// Logisim project 运算器设计 .circ as structural Verilog
// CAS
module \_8位可控加减法器  (
  input  [7:0] X,
  input  [7:0] Y,
  input  Sub,
  output [7:0] S,
  output Cout,
  output Overflow
);

  wire xor_2_out, xor_3_out, xor_4_out, xor_5_out, xor_6_out, xor_7_out, xor_8_out, xor_9_out,
       \一位全加器fa封装1_2_cout , \一位全加器fa封装1_3_cout , \一位全加器fa封装1_4_cout , \一位全加器fa封装1_5_cout ,
       \一位全加器fa封装1_6_cout , \一位全加器fa封装1_7_cout , \一位全加器fa封装1_8_cout ;
  wire [8:0] \运算指示 ;

  xor xor_1 (Overflow, \一位全加器fa封装1_2_cout , Cout);
  \一位全加器FA封装1  \u_一位全加器fa封装1_1  (.Cout(Cout), .Si(S[7]), .Cin(X[7]), .Xi(\一位全加器fa封装1_2_cout ), .Yi(xor_2_out));
  xor xor_2 (xor_2_out, Sub, Y[7]);
  \一位全加器FA封装1  \u_一位全加器fa封装1_2  (
    .Cout(\一位全加器fa封装1_2_cout ), .Si(S[6]), .Cin(X[6]), .Xi(\一位全加器fa封装1_3_cout ), .Yi(xor_3_out));
  xor xor_3 (xor_3_out, Sub, Y[6]);
  \一位全加器FA封装1  \u_一位全加器fa封装1_3  (
    .Cout(\一位全加器fa封装1_3_cout ), .Si(S[5]), .Cin(X[5]), .Xi(\一位全加器fa封装1_4_cout ), .Yi(xor_5_out));
  xor xor_4 (xor_4_out, Sub, Y[4]);
  xor xor_5 (xor_5_out, Sub, Y[5]);
  \一位全加器FA封装1  \u_一位全加器fa封装1_4  (
    .Cout(\一位全加器fa封装1_4_cout ), .Si(S[4]), .Cin(X[4]), .Xi(\一位全加器fa封装1_5_cout ), .Yi(xor_4_out));
  \一位全加器FA封装1  \u_一位全加器fa封装1_5  (
    .Cout(\一位全加器fa封装1_5_cout ), .Si(S[3]), .Cin(X[3]), .Xi(\一位全加器fa封装1_6_cout ), .Yi(xor_6_out));
  xor xor_6 (xor_6_out, Sub, Y[3]);
  \一位全加器FA封装1  \u_一位全加器fa封装1_6  (
    .Cout(\一位全加器fa封装1_6_cout ), .Si(S[2]), .Cin(X[2]), .Xi(\一位全加器fa封装1_7_cout ), .Yi(xor_7_out));
  xor xor_7 (xor_7_out, Sub, Y[2]);
  \一位全加器FA封装1  \u_一位全加器fa封装1_7  (
    .Cout(\一位全加器fa封装1_7_cout ), .Si(S[1]), .Cin(X[1]), .Xi(\一位全加器fa封装1_8_cout ), .Yi(xor_8_out));
  xor xor_8 (xor_8_out, Sub, Y[1]);
  // Probe on X
  // Probe on Y
  // Probe on S
  \一位全加器FA封装1  \u_一位全加器fa封装1_8  (.Cout(\一位全加器fa封装1_8_cout ), .Si(S[0]), .Cin(X[0]), .Xi(Sub), .Yi(xor_9_out));
  xor xor_9 (xor_9_out, Sub, Y[0]);
  DotMatrix #(.matrixcols(3), .matrixrows(3)) dotmatrix_1 (.col0(\运算指示 [8:6]), .col1(\运算指示 [5:3]), .col2(\运算指示 [2:0]));
  // Probe on X
  // Probe on Y
  // Probe on S
  Multiplexer #(.width(9), .enable("false")) multiplexer_1 (.in0(9'hba), .in1(9'h92), .out(\运算指示 ), .sel(Sub));

  // Other names for the same wires on the sheet: OF = Overflow

  // Notes on the sheet:
  //   Sub: pull=down
  //   Y: pull=down
  //   X: pull=down
  //   S: pull=down
  //   Cout: pull=down
  //   Overflow: pull=down
  //   8位可控加减法器
  //   输入引脚区
  //   输出引脚区
  //   功能说明：  8位可控加减法器    Sub=0: S = X＋Y  Sub=1:S = X－Y   Cout为最高位进位位，Overflow为有符号溢出标志
  //   =
  //   有符号
  //   =
  //   无符号
endmodule

// CLA74182
module \_4位先行进位74182  (
  input  G4,
  input  P4,
  input  G3,
  input  P3,
  input  G2,
  input  P2,
  input  G1,
  input  P1,
  input  Cin,
  output C4,
  output C3,
  output C2,
  output C1,
  output G_star,
  output P_star
);

  wire and_2_out, and_3_out, and_4_out, and_5_out, and_6_out, and_7_out, and_8_out, and_9_out, and_10_out,
       and_11_out;

  and and_1 (P_star, P4, P3, P2, P1);
  or or_1 (G_star, and_2_out, and_3_out, and_4_out, G4);
  and and_2 (and_2_out, P4, G3);
  or or_2 (C4, G4, and_2_out, and_3_out, and_4_out, and_5_out);
  and and_3 (and_3_out, P4, P3, G2);
  and and_4 (and_4_out, P4, P3, P2, G1);
  or or_3 (C3, G3, and_8_out, and_6_out, and_7_out);
  and and_5 (and_5_out, P3, P4, P2, P1, Cin);
  and and_6 (and_6_out, P3, G2);
  and and_7 (and_7_out, P3, P2, G1);
  or or_4 (C2, G2, and_9_out, and_10_out);
  and and_8 (and_8_out, P3, P2, P1, Cin);
  or or_5 (C1, G1, and_11_out);
  and and_9 (and_9_out, P2, G1);
  and and_10 (and_10_out, P2, P1, Cin);
  and and_11 (and_11_out, P1, Cin);

  // Notes on the sheet:
  //   P1: pull=down
  //   P2: pull=down
  //   Cin: pull=down
  //   G2: pull=down
  //   G3: pull=down
  //   G1: pull=down
  //   G4: pull=down
  //   P3: pull=down
  //   P4: pull=down
  //   输入引脚区
  //   4位先行进位电路
  //   请根据以上引脚以及隧道信号设计完成74LS182先行进位电路，尽可能使用多输入逻辑门，并分析电路延迟
  //   输出引脚区
endmodule

// 4位快速加法器
module \_4位快速加法器  (
  input  [3:0] X,
  input  [3:0] Y,
  input  C0,
  output [3:0] S,
  output C4,
  output C3,
  output G_star,
  output P_star
);

  wire and_1_out, and_2_out, and_3_out, and_4_out, \n4位先行进位74182_1_c1 , \n4位先行进位74182_1_c2 , xor_1_out,
       xor_4_out, xor_6_out, xor_8_out;

  \_4位先行进位74182  \u_4位先行进位74182_1  (
    .G4(and_1_out), .P4(xor_1_out), .G3(and_2_out), .P3(xor_4_out), .G2(and_3_out), .P2(xor_6_out),
    .G1(and_4_out), .P1(xor_8_out), .Cin(C0), .C4(C4), .C3(C3), .C2(\n4位先行进位74182_1_c2 ),
    .C1(\n4位先行进位74182_1_c1 ), .G_star(G_star), .P_star(P_star));
  and and_1 (and_1_out, X[3], Y[3]);
  xor xor_1 (xor_1_out, Y[3], X[3]);
  xor xor_2 (S[3], xor_1_out, C3);
  and and_2 (and_2_out, X[2], Y[2]);
  xor xor_3 (S[2], xor_4_out, \n4位先行进位74182_1_c2 );
  and and_3 (and_3_out, X[1], Y[1]);
  xor xor_4 (xor_4_out, Y[2], X[2]);
  xor xor_5 (S[1], xor_6_out, \n4位先行进位74182_1_c1 );
  xor xor_6 (xor_6_out, Y[1], X[1]);
  and and_4 (and_4_out, X[0], Y[0]);
  // Probe on X
  // Probe on Y
  // Probe on S
  xor xor_7 (S[0], xor_8_out, C0);
  xor xor_8 (xor_8_out, Y[0], X[0]);
  // Probe on X
  // Probe on Y
  // Probe on S

  // Notes on the sheet:
  //   X: pull=down
  //   C0: pull=down
  //   Y: pull=down
  //   输入引脚区
  //   4位快速加法器
  //   输出引脚区
  //   功能说明:4位Adder  S=X+Y，C4、C3分别为最高位、次高位进位位，C0为进位输入， G* P*为成组进位生成传递函数
  //   +
  //   =
  //   有符号加法
  //   +
  //   =
  //   无符号加法
endmodule

// 16位快速加法器
module \_16位快速加法器  (
  input  [15:0] X,
  input  [15:0] Y,
  input  C0,
  output C16,
  output C15,
  output G_star,
  output P_star,
  output [15:0] S
);

  wire \n4位先行进位74182_1_c1 , \n4位先行进位74182_1_c2 , \n4位先行进位74182_1_c3 , \n4位快速加法器_1_g_star ,
       \n4位快速加法器_1_p_star , \n4位快速加法器_2_c4 , \n4位快速加法器_2_g_star , \n4位快速加法器_2_p_star , \n4位快速加法器_3_g_star ,
       \n4位快速加法器_3_p_star , \n4位快速加法器_4_g_star , \n4位快速加法器_4_p_star ;

  \_4位先行进位74182  \u_4位先行进位74182_1  (
    .G4(\n4位快速加法器_1_g_star ), .P4(\n4位快速加法器_1_p_star ), .G3(\n4位快速加法器_2_g_star ), .P3(\n4位快速加法器_2_p_star ),
    .G2(\n4位快速加法器_3_g_star ), .P2(\n4位快速加法器_3_p_star ), .G1(\n4位快速加法器_4_g_star ), .P1(\n4位快速加法器_4_p_star ),
    .Cin(C0), .C4(C16), .C3(\n4位先行进位74182_1_c3 ), .C2(\n4位先行进位74182_1_c2 ), .C1(\n4位先行进位74182_1_c1 ),
    .G_star(G_star), .P_star(P_star));
  \_4位快速加法器  \u_4位快速加法器_1  (
    .X(X[15:12]), .Y(Y[15:12]), .C0(\n4位先行进位74182_1_c3 ), .S(S[15:12]), .G_star(\n4位快速加法器_1_g_star ),
    .P_star(\n4位快速加法器_1_p_star ), .C3(C15));  // open: C4
  \_4位快速加法器  \u_4位快速加法器_2  (
    .X(X[11:8]), .Y(Y[11:8]), .C0(\n4位先行进位74182_1_c2 ), .S(S[11:8]), .C4(\n4位快速加法器_2_c4 ),
    .G_star(\n4位快速加法器_2_g_star ), .P_star(\n4位快速加法器_2_p_star ));  // open: C3
  \_4位快速加法器  \u_4位快速加法器_3  (
    .X(X[7:4]), .Y(Y[7:4]), .C0(\n4位先行进位74182_1_c1 ), .S(S[7:4]), .G_star(\n4位快速加法器_3_g_star ),
    .P_star(\n4位快速加法器_3_p_star ));  // open: C4, C3
  // Probe on X
  // Probe on Y
  // Probe on S
  \_4位快速加法器  \u_4位快速加法器_4  (
    .X(X[3:0]), .Y(Y[3:0]), .C0(C0), .S(S[3:0]), .G_star(\n4位快速加法器_4_g_star ), .P_star(\n4位快速加法器_4_p_star ));  // open: C4, C3
  // Probe on X
  // Probe on Y
  // Probe on S

  // Other names for the same wires on the sheet: S0[3:0] = S[3:0]; S1[3:0] = S[7:4]; S2[3:0] = S[11:8];
  //   S3[3:0] = S[15:12]; X0[3:0] = X[3:0]; X1[3:0] = X[7:4]; X2[3:0] = X[11:8]; X3[3:0] = X[15:12]; Y0[3:0] = Y[3:0];
  //   Y1[3:0] = Y[7:4]; Y2[3:0] = Y[11:8]; Y3[3:0] = Y[15:12]

  // Notes on the sheet:
  //   C0: pull=down
  //   X: pull=down
  //   Y: pull=down
  //   输入引脚区
  //   16位快速加法器
  //   输出引脚区
  //   功能说明：16位Adder  S=X＋Y，C16、C15分别为最高位、次高位进位位，C0为进位输入， G* P*为成组进位生成传递函数
  //   +
  //   =
  //   有符号加法
  //   +
  //   =
  //   无符号加法
endmodule

// 32位加法器
module \_32位快速加法器  (
  input  C0,
  input  [31:0] X,
  input  [31:0] Y,
  output C32,
  output C31,
  output [31:0] S
);

  wire \n4位先行进位74182_1_c1 , \n4位先行进位74182_1_c2 , \n4位先行进位74182_1_c3 , \n4位先行进位74182_2_c1 ,
       \n4位先行进位74182_2_c2 , \n4位先行进位74182_2_c3 , \n4位先行进位74182_2_c4 , \n4位快速加法器_1_g_star ,
       \n4位快速加法器_1_p_star , \n4位快速加法器_2_g_star , \n4位快速加法器_2_p_star , \n4位快速加法器_3_g_star ,
       \n4位快速加法器_3_p_star , \n4位快速加法器_4_g_star , \n4位快速加法器_4_p_star , \n4位快速加法器_5_g_star ,
       \n4位快速加法器_5_p_star , \n4位快速加法器_6_g_star , \n4位快速加法器_6_p_star , \n4位快速加法器_7_g_star ,
       \n4位快速加法器_7_p_star , \n4位快速加法器_8_g_star , \n4位快速加法器_8_p_star ;

  \_4位先行进位74182  \u_4位先行进位74182_1  (
    .G4(\n4位快速加法器_1_g_star ), .P4(\n4位快速加法器_1_p_star ), .G3(\n4位快速加法器_2_g_star ), .P3(\n4位快速加法器_2_p_star ),
    .G2(\n4位快速加法器_3_g_star ), .P2(\n4位快速加法器_3_p_star ), .G1(\n4位快速加法器_4_g_star ), .P1(\n4位快速加法器_4_p_star ),
    .Cin(\n4位先行进位74182_2_c4 ), .C4(C32), .C3(\n4位先行进位74182_1_c3 ), .C2(\n4位先行进位74182_1_c2 ),
    .C1(\n4位先行进位74182_1_c1 ));  // open: G_star, P_star
  \_4位快速加法器  \u_4位快速加法器_1  (
    .X(X[31:28]), .Y(Y[31:28]), .C0(\n4位先行进位74182_1_c3 ), .S(S[31:28]), .G_star(\n4位快速加法器_1_g_star ),
    .P_star(\n4位快速加法器_1_p_star ), .C3(C31));  // open: C4
  \_4位快速加法器  \u_4位快速加法器_2  (
    .X(X[27:24]), .Y(Y[27:24]), .C0(\n4位先行进位74182_1_c2 ), .S(S[27:24]), .G_star(\n4位快速加法器_2_g_star ),
    .P_star(\n4位快速加法器_2_p_star ));  // open: C4, C3
  \_4位快速加法器  \u_4位快速加法器_3  (
    .X(X[23:20]), .Y(Y[23:20]), .C0(\n4位先行进位74182_1_c1 ), .S(S[23:20]), .G_star(\n4位快速加法器_3_g_star ),
    .P_star(\n4位快速加法器_3_p_star ));  // open: C4, C3
  // Probe on X
  // Probe on Y
  // Probe on S
  \_4位快速加法器  \u_4位快速加法器_4  (
    .X(X[19:16]), .Y(Y[19:16]), .C0(\n4位先行进位74182_2_c4 ), .S(S[19:16]), .G_star(\n4位快速加法器_4_g_star ),
    .P_star(\n4位快速加法器_4_p_star ));  // open: C4, C3
  \_4位先行进位74182  \u_4位先行进位74182_2  (
    .G4(\n4位快速加法器_5_g_star ), .P4(\n4位快速加法器_5_p_star ), .G3(\n4位快速加法器_6_g_star ), .P3(\n4位快速加法器_6_p_star ),
    .G2(\n4位快速加法器_7_g_star ), .P2(\n4位快速加法器_7_p_star ), .G1(\n4位快速加法器_8_g_star ), .P1(\n4位快速加法器_8_p_star ),
    .Cin(C0), .C4(\n4位先行进位74182_2_c4 ), .C3(\n4位先行进位74182_2_c3 ), .C2(\n4位先行进位74182_2_c2 ),
    .C1(\n4位先行进位74182_2_c1 ));  // open: G_star, P_star
  // Probe on X
  // Probe on Y
  // Probe on S
  \_4位快速加法器  \u_4位快速加法器_5  (
    .X(X[15:12]), .Y(Y[15:12]), .C0(\n4位先行进位74182_2_c3 ), .S(S[15:12]), .G_star(\n4位快速加法器_5_g_star ),
    .P_star(\n4位快速加法器_5_p_star ));  // open: C4, C3
  \_4位快速加法器  \u_4位快速加法器_6  (
    .X(X[11:8]), .Y(Y[11:8]), .C0(\n4位先行进位74182_2_c2 ), .S(S[11:8]), .G_star(\n4位快速加法器_6_g_star ),
    .P_star(\n4位快速加法器_6_p_star ));  // open: C4, C3
  \_4位快速加法器  \u_4位快速加法器_7  (
    .X(X[7:4]), .Y(Y[7:4]), .C0(\n4位先行进位74182_2_c1 ), .S(S[7:4]), .G_star(\n4位快速加法器_7_g_star ),
    .P_star(\n4位快速加法器_7_p_star ));  // open: C4, C3
  \_4位快速加法器  \u_4位快速加法器_8  (
    .X(X[3:0]), .Y(Y[3:0]), .C0(C0), .S(S[3:0]), .G_star(\n4位快速加法器_8_g_star ), .P_star(\n4位快速加法器_8_p_star ));  // open: C4, C3

  // Other names for the same wires on the sheet: S0[3:0] = S[3:0]; S1[3:0] = S[7:4]; S2[3:0] = S[11:8];
  //   S3[3:0] = S[15:12]; S4[3:0] = S[19:16]; S5[3:0] = S[23:20]; S6[3:0] = S[27:24]; S7[3:0] = S[31:28];
  //   X0[3:0] = X[3:0]; X1[3:0] = X[7:4]; X2[3:0] = X[11:8]; X3[3:0] = X[15:12]; X4[3:0] = X[19:16];
  //   X5[3:0] = X[23:20]; X6[3:0] = X[27:24]; X7[3:0] = X[31:28]; Y0[3:0] = Y[3:0]; Y1[3:0] = Y[7:4];
  //   Y2[3:0] = Y[11:8]; Y3[3:0] = Y[15:12]; Y4[3:0] = Y[19:16]; Y5[3:0] = Y[23:20]; Y6[3:0] = Y[27:24];
  //   Y7[3:0] = Y[31:28]

  // Notes on the sheet:
  //   X: pull=down
  //   C0: pull=down
  //   Y: pull=down
  //   输入引脚区
  //   32位快速加法器
  //   功能说明：利用已完成的74182以及4位快速加法器构建速度最快的32位加法器 S = X ＋ Y，并分析电路延迟；
  //   输出引脚区
  //   +
  //   =
  //   有符号加法
  //   +
  //   =
  //   无符号加法
  //   C32、C31分别为最高位、次高位进位位，C0为进位输入
endmodule

// 5位阵列乘法器
module \_5位阵列乘法器  (
  input  [4:0] X,
  input  [4:0] Y,
  output [9:0] \乘积 
);

  wire X0Y1, X0Y2, X0Y3, X0Y4, X1Y0, X1Y1, X1Y2, X1Y3, X1Y4, X2Y0, X2Y1, X2Y2, X2Y3, X2Y4, X3Y0, X3Y1, X3Y2,
       X3Y3, X3Y4, X4Y0, X4Y1, X4Y2, X4Y3, X4Y4, \一位全加器fa封装3_2_cout , \一位全加器fa封装3_2_si , \一位全加器fa封装3_3_cout ,
       \一位全加器fa封装3_4_cout , \一位全加器fa封装3_4_si , \一位全加器fa封装3_5_cout , \一位全加器fa封装3_5_si , \一位全加器fa封装3_6_cout ,
       \一位全加器fa封装3_7_cout , \一位全加器fa封装3_7_si , \一位全加器fa封装3_8_cout , \一位全加器fa封装3_8_si , \一位全加器fa封装3_9_cout ,
       \一位全加器fa封装3_9_si , \一位全加器fa封装3_10_cout , \一位全加器fa封装3_11_cout , \一位全加器fa封装3_11_si ,
       \一位全加器fa封装3_12_cout , \一位全加器fa封装3_12_si , \一位全加器fa封装3_13_cout , \一位全加器fa封装3_13_si ,
       \一位全加器fa封装3_14_cout , \一位全加器fa封装3_15_cout , \一位全加器fa封装3_15_si , \一位全加器fa封装3_16_cout ,
       \一位全加器fa封装3_16_si , \一位全加器fa封装3_17_cout , \一位全加器fa封装3_18_cout , \一位全加器fa封装3_18_si ,
       \一位全加器fa封装3_19_cout , \一位全加器fa封装3_20_cout ;

  \一位全加器FA封装3  \u_一位全加器fa封装3_1  (
    .Cout(\乘积 [9]), .Si(\乘积 [8]), .Cin(\一位全加器fa封装3_2_cout ), .Xi(\一位全加器fa封装3_3_cout ), .Yi(X4Y4));
  // Probe on X
  \一位全加器FA封装3  \u_一位全加器fa封装3_2  (
    .Cout(\一位全加器fa封装3_2_cout ), .Si(\一位全加器fa封装3_2_si ), .Cin(\一位全加器fa封装3_4_cout ), .Xi(X3Y4), .Yi(X4Y3));
  \一位全加器FA封装3  \u_一位全加器fa封装3_3  (
    .Cout(\一位全加器fa封装3_3_cout ), .Si(\乘积 [7]), .Cin(\一位全加器fa封装3_5_cout ), .Xi(\一位全加器fa封装3_6_cout ),
    .Yi(\一位全加器fa封装3_2_si ));
  \一位全加器FA封装3  \u_一位全加器fa封装3_4  (
    .Cout(\一位全加器fa封装3_4_cout ), .Si(\一位全加器fa封装3_4_si ), .Cin(\一位全加器fa封装3_7_cout ), .Xi(X3Y3), .Yi(X4Y2));
  \一位全加器FA封装3  \u_一位全加器fa封装3_5  (
    .Cout(\一位全加器fa封装3_5_cout ), .Si(\一位全加器fa封装3_5_si ), .Cin(\一位全加器fa封装3_8_cout ), .Xi(X2Y4),
    .Yi(\一位全加器fa封装3_4_si ));
  \一位全加器FA封装3  \u_一位全加器fa封装3_6  (
    .Cout(\一位全加器fa封装3_6_cout ), .Si(\乘积 [6]), .Cin(\一位全加器fa封装3_9_cout ), .Xi(\一位全加器fa封装3_10_cout ),
    .Yi(\一位全加器fa封装3_5_si ));
  // Probe on Y
  \一位全加器FA封装3  \u_一位全加器fa封装3_7  (
    .Cout(\一位全加器fa封装3_7_cout ), .Si(\一位全加器fa封装3_7_si ), .Cin(\一位全加器fa封装3_11_cout ), .Xi(X3Y2), .Yi(X4Y1));
  \一位全加器FA封装3  \u_一位全加器fa封装3_8  (
    .Cout(\一位全加器fa封装3_8_cout ), .Si(\一位全加器fa封装3_8_si ), .Cin(\一位全加器fa封装3_12_cout ), .Xi(X2Y3),
    .Yi(\一位全加器fa封装3_7_si ));
  \一位全加器FA封装3  \u_一位全加器fa封装3_9  (
    .Cout(\一位全加器fa封装3_9_cout ), .Si(\一位全加器fa封装3_9_si ), .Cin(\一位全加器fa封装3_13_cout ), .Xi(X1Y4),
    .Yi(\一位全加器fa封装3_8_si ));
  \一位全加器FA封装3  \u_一位全加器fa封装3_10  (
    .Cout(\一位全加器fa封装3_10_cout ), .Si(\乘积 [5]), .Cin(\一位全加器fa封装3_14_cout ), .Xi(1'b0), .Yi(\一位全加器fa封装3_9_si ));
  \一位全加器FA封装3  \u_一位全加器fa封装3_11  (
    .Cout(\一位全加器fa封装3_11_cout ), .Si(\一位全加器fa封装3_11_si ), .Cin(1'b0), .Xi(X3Y1), .Yi(X4Y0));
  \一位全加器FA封装3  \u_一位全加器fa封装3_12  (
    .Cout(\一位全加器fa封装3_12_cout ), .Si(\一位全加器fa封装3_12_si ), .Cin(\一位全加器fa封装3_15_cout ), .Xi(X2Y2),
    .Yi(\一位全加器fa封装3_11_si ));
  \一位全加器FA封装3  \u_一位全加器fa封装3_13  (
    .Cout(\一位全加器fa封装3_13_cout ), .Si(\一位全加器fa封装3_13_si ), .Cin(\一位全加器fa封装3_16_cout ), .Xi(X1Y3),
    .Yi(\一位全加器fa封装3_12_si ));
  \一位全加器FA封装3  \u_一位全加器fa封装3_14  (
    .Cout(\一位全加器fa封装3_14_cout ), .Si(\乘积 [4]), .Cin(\一位全加器fa封装3_17_cout ), .Xi(X0Y4), .Yi(\一位全加器fa封装3_13_si ));
  \一位全加器FA封装3  \u_一位全加器fa封装3_15  (
    .Cout(\一位全加器fa封装3_15_cout ), .Si(\一位全加器fa封装3_15_si ), .Cin(1'b0), .Xi(X2Y1), .Yi(X3Y0));
  \一位全加器FA封装3  \u_一位全加器fa封装3_16  (
    .Cout(\一位全加器fa封装3_16_cout ), .Si(\一位全加器fa封装3_16_si ), .Cin(\一位全加器fa封装3_18_cout ), .Xi(X1Y2),
    .Yi(\一位全加器fa封装3_15_si ));
  \一位全加器FA封装3  \u_一位全加器fa封装3_17  (
    .Cout(\一位全加器fa封装3_17_cout ), .Si(\乘积 [3]), .Cin(\一位全加器fa封装3_19_cout ), .Xi(X0Y3), .Yi(\一位全加器fa封装3_16_si ));
  \一位全加器FA封装3  \u_一位全加器fa封装3_18  (
    .Cout(\一位全加器fa封装3_18_cout ), .Si(\一位全加器fa封装3_18_si ), .Cin(1'b0), .Xi(X1Y1), .Yi(X2Y0));
  \一位全加器FA封装3  \u_一位全加器fa封装3_19  (
    .Cout(\一位全加器fa封装3_19_cout ), .Si(\乘积 [2]), .Cin(\一位全加器fa封装3_20_cout ), .Xi(X0Y2), .Yi(\一位全加器fa封装3_18_si ));
  // Probe on X
  // Probe on Y
  // Probe on \乘积 
  \一位全加器FA封装3  \u_一位全加器fa封装3_20  (.Cout(\一位全加器fa封装3_20_cout ), .Si(\乘积 [1]), .Cin(1'b0), .Xi(X0Y1), .Yi(X1Y0));
  \_5位乘法与门阵列  \u_5位乘法与门阵列_1  (
    .X(X), .XY4({X4Y4, X3Y4, X2Y4, X1Y4, X0Y4}), .XY3({X4Y3, X3Y3, X2Y3, X1Y3, X0Y3}),
    .XY2({X4Y2, X3Y2, X2Y2, X1Y2, X0Y2}), .XY1({X4Y1, X3Y1, X2Y1, X1Y1, X0Y1}),
    .XY0({X4Y0, X3Y0, X2Y0, X1Y0, \乘积 [0]}), .Y(Y));

  // Other names for the same wires on the sheet: P[9:0] = \乘积 ; P1 = \乘积 [1]; P2 = \乘积 [2]; P3 = \乘积 [3];
  //   P4 = \乘积 [4]; P5 = \乘积 [5]; P6 = \乘积 [6]; P7 = \乘积 [7]; P8 = \乘积 [8]; P9 = \乘积 [9]; P0 = \乘积 [0];
  //   X0Y0 = \乘积 [0]; XY0[4:0] = {X4Y0, X3Y0, X2Y0, X1Y0, \乘积 [0]}; XY1[4:0] = {X4Y1, X3Y1, X2Y1, X1Y1, X0Y1};
  //   XY2[4:0] = {X4Y2, X3Y2, X2Y2, X1Y2, X0Y2}; XY3[4:0] = {X4Y3, X3Y3, X2Y3, X1Y3, X0Y3};
  //   XY4[4:0] = {X4Y4, X3Y4, X2Y4, X1Y4, X0Y4}

  // Notes on the sheet:
  //   X: pull=down
  //   Y: pull=down
  //   5位无符号阵列乘法器
  //   输入引脚区
  //   功能说明：利用一位全加器构成5位×5位的无符号数阵列乘法器，乘积=X×Y，并分析电路延迟；
  //   输出引脚区
  //   ×
  //   =
endmodule

module \_6位补码阵列乘法器  (
  input  [5:0] X,
  input  [5:0] Y,
  output [10:0] \乘积 
);

  wire [4:0] X_t, Y_t;
  wire [5:0] negator_1_out, negator_3_out;
  wire [9:0] \n5位阵列乘法器_1_乘积 , negator_2_out;

  // Probe on X
  \_5位阵列乘法器  \u_5位阵列乘法器_1  (.\乘积 (\n5位阵列乘法器_1_乘积 ), .X(X_t), .Y(Y_t));
  Negator #(.width(6)) negator_1 (.in(X), .out(negator_1_out));
  // Probe on Y
  // Probe on X_t
  Multiplexer #(.width(5), .enable("false")) multiplexer_1 (
    .in0(X[4:0]), .in1(negator_1_out[4:0]), .out(X_t), .sel(X[5]));
  Negator #(.width(10)) negator_2 (.in(\n5位阵列乘法器_1_乘积 ), .out(negator_2_out));
  Negator #(.width(6)) negator_3 (.in(Y), .out(negator_3_out));
  xor xor_1 (\乘积 [10], Y[5], X[5]);
  Multiplexer #(.width(5), .enable("false")) multiplexer_2 (
    .in0(Y[4:0]), .in1(negator_3_out[4:0]), .out(Y_t), .sel(Y[5]));
  Multiplexer #(.width(10), .enable("false")) multiplexer_3 (
    .in0(\n5位阵列乘法器_1_乘积 ), .in1(negator_2_out), .out(\乘积 [9:0]), .sel(\乘积 [10]));
  // Probe on Y_t
  // Probe on X
  // Probe on Y
  // Probe on \乘积 

  // Other names for the same wires on the sheet: P[10:0] = \乘积 ; P0 = \乘积 [0]; P1 = \乘积 [1]; P2 = \乘积 [2];
  //   P3 = \乘积 [3]; P4 = \乘积 [4]; P5 = \乘积 [5]; P6 = \乘积 [6]; P7 = \乘积 [7]; P8 = \乘积 [8]; P9 = \乘积 [9];
  //   P10 = \乘积 [10]; X4_0[4:0] = X[4:0]; Y4_0[4:0] = Y[4:0]

  // Notes on the sheet:
  //   6位补码阵列乘法器
  //   输入引脚区
  //   功能说明：利用五位阵列乘法器6位×6位的补码阵列乘法器，乘积P = X × Y，尝试计算 －32 × 1，分析结果  
  //   输出引脚区
  //   ×
  //   =
endmodule

module \_5位无符号乘法流水线  (
  output [4:0] X,
  output [9:0] P2,
  output [9:0] P3,
  output [9:0] P4,
  output [9:0] P5,
  output [4:0] Y
);

  wire CLK, comparator_1_eq, not_1_out, OK;
  wire [4:0] \n5位乘法与门阵列_1_xy0 , \n5位乘法与门阵列_1_xy1 , \n5位乘法与门阵列_1_xy2 , \n5位乘法与门阵列_1_xy3 , \n5位乘法与门阵列_1_xy4 ,
       X_t, Y_t, \乘法线流水接口_1_x_prime , \乘法线流水接口_1_xy0_prime , \乘法线流水接口_1_xy1_prime , \乘法线流水接口_1_xy2_prime ,
       \乘法线流水接口_1_xy3_2 , \乘法线流水接口_1_xy4_2 , \乘法线流水接口_1_y_prime , \乘法线流水接口_2_x_prime , \乘法线流水接口_2_xy0_prime ,
       \乘法线流水接口_2_xy1_prime , \乘法线流水接口_2_xy2_prime , \乘法线流水接口_2_xy3_2 , \乘法线流水接口_2_xy4_2 ,
       \乘法线流水接口_2_y_prime , \乘法线流水接口_3_x_prime , \乘法线流水接口_3_xy0_prime , \乘法线流水接口_3_xy1_prime ,
       \乘法线流水接口_3_xy2_prime , \乘法线流水接口_3_xy3_2 , \乘法线流水接口_3_xy4_2 , \乘法线流水接口_3_y_prime , \乘法线流水接口_4_x_prime ,
       \乘法线流水接口_4_y_prime ;
  wire [5:0] counter_1_q;
  wire [9:0] adder_1_out, adder_2_out, adder_3_out, adder_4_out, bit_extender_1_out, bit_extender_2_out,
       bit_extender_3_out, bit_extender_4_out, bit_extender_5_out, multiplier_1_out, P, shifter_1_out,
       shifter_2_out, shifter_3_out, shifter_4_out, \乘法线流水接口_1_out_19 , \乘法线流水接口_2_out_19 ,
       \乘法线流水接口_3_out_19 , \乘法线流水接口_4_out_19 ;

  Clock clock_1 (.out(CLK));
  Counter #(.width(6), .max('h3f)) counter_1 (.Q(counter_1_q), .clk(CLK));  // open: load, D, count, carry, clr
  \_5位乘法与门阵列  \u_5位乘法与门阵列_1  (
    .X(X), .XY4(\n5位乘法与门阵列_1_xy4 ), .XY3(\n5位乘法与门阵列_1_xy3 ), .XY2(\n5位乘法与门阵列_1_xy2 ),
    .XY1(\n5位乘法与门阵列_1_xy1 ), .XY0(\n5位乘法与门阵列_1_xy0 ), .Y(Y));
  // Probe on X
  ROM #(.addrWidth(6), .dataWidth(10)) rom_1 (.addr(counter_1_q), .data({Y, X}));  // open: sel
  // Probe on Y
  assign bit_extender_1_out = {{5{1'b0}}, \n5位乘法与门阵列_1_xy0 };  // Bit_Extender bit_extender_1
  assign bit_extender_2_out = {{5{1'b0}}, \n5位乘法与门阵列_1_xy1 };  // Bit_Extender bit_extender_2
  Shifter #(.width(10)) shifter_1 (.in(bit_extender_2_out), .\dist (4'b0001), .out(shifter_1_out));
  Adder #(.width(10)) adder_1 (.a(bit_extender_1_out), .b(shifter_1_out), .out(adder_1_out));  // open: cin, cout
  \乘法线流水接口  \u_乘法线流水接口_1  (
    .X(X), .Y(Y), .XY0(\n5位乘法与门阵列_1_xy0 ), .XY1(\n5位乘法与门阵列_1_xy1 ), .XY2(\n5位乘法与门阵列_1_xy2 ),
    .XY3(\n5位乘法与门阵列_1_xy3 ), .XY4(\n5位乘法与门阵列_1_xy4 ), .in_8(adder_1_out), .CLK(CLK),
    .X_prime(\乘法线流水接口_1_x_prime ), .Y_prime(\乘法线流水接口_1_y_prime ), .XY0_prime(\乘法线流水接口_1_xy0_prime ),
    .XY1_prime(\乘法线流水接口_1_xy1_prime ), .XY2_prime(\乘法线流水接口_1_xy2_prime ), .XY3_2(\乘法线流水接口_1_xy3_2 ),
    .XY4_2(\乘法线流水接口_1_xy4_2 ), .out_19(\乘法线流水接口_1_out_19 ), .EDU(P2));  // open: 同步清零_高电平有效, 使能端_低电平有效
  // Probe on \乘法线流水接口_1_x_prime 
  assign bit_extender_3_out = {{5{1'b0}}, \乘法线流水接口_1_xy2_prime };  // Bit_Extender bit_extender_3
  // Probe on X_t
  // Probe on Y_t
  // Probe on P
  // Probe on \乘法线流水接口_1_y_prime 
  Shifter #(.width(10)) shifter_2 (.in(bit_extender_3_out), .\dist (4'b0010), .out(shifter_2_out));
  \乘法线流水接口  \u_乘法线流水接口_2  (
    .X(\乘法线流水接口_1_x_prime ), .Y(\乘法线流水接口_1_y_prime ), .XY0(\乘法线流水接口_1_xy0_prime ),
    .XY1(\乘法线流水接口_1_xy1_prime ), .XY2(\乘法线流水接口_1_xy2_prime ), .XY3(\乘法线流水接口_1_xy3_2 ),
    .XY4(\乘法线流水接口_1_xy4_2 ), .in_8(adder_2_out), .CLK(CLK), .X_prime(\乘法线流水接口_2_x_prime ),
    .Y_prime(\乘法线流水接口_2_y_prime ), .XY0_prime(\乘法线流水接口_2_xy0_prime ), .XY1_prime(\乘法线流水接口_2_xy1_prime ),
    .XY2_prime(\乘法线流水接口_2_xy2_prime ), .XY3_2(\乘法线流水接口_2_xy3_2 ), .XY4_2(\乘法线流水接口_2_xy4_2 ),
    .out_19(\乘法线流水接口_2_out_19 ), .EDU(P3));  // open: 同步清零_高电平有效, 使能端_低电平有效
  Adder #(.width(10)) adder_2 (.a(shifter_2_out), .b(\乘法线流水接口_1_out_19 ), .out(adder_2_out));  // open: cin, cout
  LED led_1 (.in(OK));
  // Probe on \乘法线流水接口_2_x_prime 
  assign bit_extender_4_out = {{5{1'b0}}, \乘法线流水接口_2_xy3_2 };  // Bit_Extender bit_extender_4
  Shifter #(.width(10)) shifter_3 (.in(bit_extender_4_out), .\dist (4'b0011), .out(shifter_3_out));
  // Probe on \乘法线流水接口_2_y_prime 
  Adder #(.width(10)) adder_3 (.a(shifter_3_out), .b(\乘法线流水接口_2_out_19 ), .out(adder_3_out));  // open: cin, cout
  \乘法线流水接口  \u_乘法线流水接口_3  (
    .X(\乘法线流水接口_2_x_prime ), .Y(\乘法线流水接口_2_y_prime ), .XY0(\乘法线流水接口_2_xy0_prime ),
    .XY1(\乘法线流水接口_2_xy1_prime ), .XY2(\乘法线流水接口_2_xy2_prime ), .XY3(\乘法线流水接口_2_xy3_2 ),
    .XY4(\乘法线流水接口_2_xy4_2 ), .in_8(adder_3_out), .CLK(CLK), .X_prime(\乘法线流水接口_3_x_prime ),
    .Y_prime(\乘法线流水接口_3_y_prime ), .XY0_prime(\乘法线流水接口_3_xy0_prime ), .XY1_prime(\乘法线流水接口_3_xy1_prime ),
    .XY2_prime(\乘法线流水接口_3_xy2_prime ), .XY3_2(\乘法线流水接口_3_xy3_2 ), .XY4_2(\乘法线流水接口_3_xy4_2 ),
    .out_19(\乘法线流水接口_3_out_19 ), .EDU(P4));  // open: 同步清零_高电平有效, 使能端_低电平有效
  // Probe on \乘法线流水接口_3_x_prime 
  assign bit_extender_5_out = {{5{1'b0}}, \乘法线流水接口_3_xy4_2 };  // Bit_Extender bit_extender_5
  // Probe on \乘法线流水接口_3_y_prime 
  Shifter #(.width(10)) shifter_4 (.in(bit_extender_5_out), .\dist (4'b0100), .out(shifter_4_out));
  \乘法线流水接口  \u_乘法线流水接口_4  (
    .X(\乘法线流水接口_3_x_prime ), .Y(\乘法线流水接口_3_y_prime ), .XY0(\乘法线流水接口_3_xy0_prime ),
    .XY1(\乘法线流水接口_3_xy1_prime ), .XY2(\乘法线流水接口_3_xy2_prime ), .XY3(\乘法线流水接口_3_xy3_2 ),
    .XY4(\乘法线流水接口_3_xy4_2 ), .in_8(adder_4_out), .CLK(CLK), .X_prime(\乘法线流水接口_4_x_prime ),
    .Y_prime(\乘法线流水接口_4_y_prime ), .out_19(\乘法线流水接口_4_out_19 ), .EDU(P5));  // open: XY0_prime, XY1_prime, XY2_prime, XY3_2, XY4_2, 同步清零_高电平有效, 使能端_低电平有效
  Adder #(.width(10)) adder_4 (.a(shifter_4_out), .b(\乘法线流水接口_3_out_19 ), .out(adder_4_out));  // open: cin, cout
  // Probe on \乘法线流水接口_4_x_prime 
  // Probe on \乘法线流水接口_4_y_prime 
  // Probe on multiplier_1_out
  // Probe on \乘法线流水接口_4_out_19 
  Multiplier #(.width(5)) multiplier_1 (
    .a(\乘法线流水接口_4_x_prime ), .b(\乘法线流水接口_4_y_prime ), .out(multiplier_1_out[4:0]),
    .cout(multiplier_1_out[9:5]));  // open: cin
  Comparator #(.width(10)) comparator_1 (
    .a(multiplier_1_out), .b(\乘法线流水接口_4_out_19 ), .eq(comparator_1_eq));  // open: gt, lt
  not not_1 (not_1_out, comparator_1_eq);
  LED \u_不正确  (.in(not_1_out));

  // Other names for the same wires on the sheet: 被乘数X[4:0] = X; 乘数Y[4:0] = Y

  // Notes on the sheet:
  //   contents of rom_1 (hex, n*v repeats v):
  //   3fe 58 23 1e 2c 34 66 380 3c0 55 3b3 12 18 3dc 390 390 3b9 45 1e 398 21 14 5c 6 3d2 3aa 41 28 394
  //   38c 5a 3f8 28 1c 48 3b4 3b2 45 3bc 0 399 3e0 26 44 69 55 8 3e0 8 4b 38a 0 3b4 1a 78 393 0 18 40 3b0
  //   390 3f0 7e 50
  //   第1步
  //   ×
  //   =
  //   第2步
  //   第3步
  //   第4步
endmodule

module \原码一位乘法器  (
  input  [7:0] X,
  input  [7:0] Y,
  output [15:0] \乘积 
);

  wire comparator_1_eq, comparator_2_lt, RST, \时钟_out ;
  wire [0:0] \n8位串行加法器_1_s ;
  wire [7:0] counter_1_q, multiplexer_1_out, multiplexer_2_out, \n8位串行加法器_1_cout ;

  Clock \u_时钟  (.out(\时钟_out ));
  Button \u_复位  (.out(RST));
  // Probe on \乘积 [15:8]
  Register register_1 (.D(\n8位串行加法器_1_cout ), .en(comparator_2_lt), .Q(\乘积 [15:8]), .clk(\时钟_out ), .clr(RST));
  \_8位串行加法器  \u_8位串行加法器_1  (
    .X(\乘积 [15:8]), .Y(multiplexer_1_out), .S({\n8位串行加法器_1_cout [6:0], \n8位串行加法器_1_s [0]}),
    .Cout(\n8位串行加法器_1_cout [7]));  // open: Cin, Overflow
  // Probe on \乘积 [7:0]
  Register Y_2 (.D(multiplexer_2_out), .en(comparator_2_lt), .Q(\乘积 [7:0]), .clk(\时钟_out ), .clr(RST));
  Multiplexer #(.width(8), .enable("false")) multiplexer_1 (
    .in0({8{1'b0}}), .in1(X), .out(multiplexer_1_out), .sel(\乘积 [0]));
  Counter counter_1 (.Q(counter_1_q), .clk(\时钟_out ), .clr(RST));  // open: load, D, count, carry
  // Probe on X
  // Probe on Y
  // Probe on \乘积 
  Multiplexer #(.width(8), .enable("false")) multiplexer_2 (
    .in0({\n8位串行加法器_1_s [0], \乘积 [7:1]}), .in1(Y), .out(multiplexer_2_out), .sel(comparator_1_eq));
  Comparator #(.mode("unsigned")) comparator_1 (.a(counter_1_q), .b({8{1'b0}}), .eq(comparator_1_eq));  // open: gt, lt
  Comparator #(.mode("unsigned")) comparator_2 (.a(counter_1_q), .b(8'h9), .lt(comparator_2_lt));  // open: gt, eq

  // Notes on the sheet:
  //   8位无符号一位乘法器
  //   ∑
  //   功能说明: 原码一位乘法器   乘积=X*Y，要求采用原码一位乘法实现，最终结果能输出在乘积引脚上
  //   逻辑右移一位
  //   ∑+Yn|X|
  //   后续所有实验中凡是涉及存储器件，如寄存器、计数器、RAM等，必须增加统一的复位信号RST，方便系统复位
  //   输入输出引脚区
  //   ×
  //   =
  //   核心算法：{ ∑ , Y } = { ∑ ＋ Y  |X|  , Y  } / 2
  //   n
endmodule

module \补码一位乘法器  (
  input  [7:0] X,
  input  [7:0] Y,
  output [15:0] \乘积 
);

  wire clock_1_out, comparator_1_eq, comparator_2_lt, RST;
  wire [0:0] \n8位串行加法器_1_s_2 , Yn_1_2_q;
  wire [5:0] counter_1_q;
  wire [7:0] multiplexer_1_out, multiplexer_2_out, \n8位串行加法器_1_s , negator_1_out;

  Clock clock_1 (.out(clock_1_out));
  Register register (
    .D({{2{\n8位串行加法器_1_s [7]}}, \n8位串行加法器_1_s [5:0]}), .en(comparator_2_lt), .Q(\乘积 [15:8]),
    .clk(clock_1_out), .clr(RST));
  Button \u_复位  (.out(RST));
  // Probe on \乘积 [15:8]
  \_8位串行加法器  \u_8位串行加法器_1  (
    .X(\乘积 [15:8]), .Y(multiplexer_1_out), .S({\n8位串行加法器_1_s [7], \n8位串行加法器_1_s [5:0], \n8位串行加法器_1_s_2 [0]}));  // open: Cin, Cout, Overflow
  // Probe on \乘积 [7:0]
  Register Y_2 (.D(multiplexer_2_out), .en(comparator_2_lt), .Q(\乘积 [7:0]), .clk(clock_1_out), .clr(RST));
  Multiplexer #(.select(2), .width(8), .enable("false")) multiplexer_1 (
    .in0({8{1'b0}}), .in1(X), .in2(negator_1_out), .in3({8{1'b0}}), .out(multiplexer_1_out),
    .sel({\乘积 [0], Yn_1_2_q[0]}));
  // Probe on Yn_1_2_q[0]
  Register #(.width(1)) Yn_1_2 (.D(\乘积 [0]), .en(comparator_2_lt), .Q(Yn_1_2_q[0]), .clk(clock_1_out), .clr(RST));
  Negator negator_1 (.in(X), .out(negator_1_out));
  // Probe on X
  // Probe on Y
  // Probe on \乘积 
  Counter #(.width(6), .max('h3f)) counter_1 (.Q(counter_1_q), .clk(clock_1_out));  // open: load, D, count, carry, clr
  Comparator #(.width(6)) comparator_1 (.a(counter_1_q), .b({6{1'b0}}), .eq(comparator_1_eq));  // open: gt, lt
  Comparator #(.width(6)) comparator_2 (.a(counter_1_q), .b(6'b001001), .lt(comparator_2_lt));  // open: gt, eq
  Multiplexer #(.width(8), .enable("false")) multiplexer_2 (
    .in0({\n8位串行加法器_1_s_2 [0], \乘积 [7:1]}), .in1(Y), .out(multiplexer_2_out), .sel(comparator_1_eq));

  // Notes on the sheet:
  //   8位补码 Booth一位乘法器
  //   功能说明: 补码一位乘法器   乘积=X×Y，要求采用补码一位乘法实现，最终结果能输出在乘积引脚上
  //   算术右移一位
  //   ∑+ (Yn+1-Yn)补
  //   ∑+=(Yn+1-Yn)[X]补/2
  //   输入输出引脚区
  //   核心算法：{ ∑,Y } = { ∑ ＋（Y      －  Y  ）[X]   , Y } / 2
  //   ×
  //   =
  //   n
  //   n+1
  //   补
endmodule

// ALU
module \算术逻辑运算单元ALU  (
  input  [31:0] X,
  input  [31:0] Y,
  input  [3:0] AluOP,
  output Signed_Overflow,
  output UnSigned_Overflow,
  output Equal,
  output [31:0] Result,
  output [31:0] Result_2
);

  wire comparator_1_lt, comparator_2_lt, \n32位快速加法器_2_c31 , \n32位快速加法器_2_c32 , \n32位快速加法器_4_c31 ,
       \n32位快速加法器_4_c32 , \n32位快速加法器_5_c32 , \n32位快速加法器_6_c32 , not_1_out, xor_2_out, xor_3_out;
  wire [31:0] and_1_out, divider_1_out, divider_1_rem, multiplexer_1_out, multiplexer_2_out,
       multiplier_1_cout, multiplier_1_out, \n32位快速加法器_1_s , \n32位快速加法器_3_s , negator_1_out, negator_2_out,
       negator_3_out, nor_1_out, or_1_out, shifter_1_out, shifter_2_out, shifter_3_out, xor_1_out;

  // Probe on X
  // Probe on X
  Comparator #(.width(32), .mode("unsigned")) comparator_1 (.a(Y), .b(X), .lt(comparator_1_lt));  // open: gt, eq
  Comparator #(.width(32)) comparator_2 (.a(Y), .b(X), .lt(comparator_2_lt));  // open: gt, eq
  assign nor_1_out = ~(Y | X);  // NOR_Gate nor_1, 32 bits wide
  assign xor_1_out = Y ^ X;  // XOR_Gate xor_1, 32 bits wide
  assign or_1_out = Y | X;  // OR_Gate or_1, 32 bits wide
  assign and_1_out = Y & X;  // AND_Gate and_1, 32 bits wide
  Comparator #(.width(32)) comparator_3 (.a(X), .b(Y), .eq(Equal));  // open: gt, lt
  // Probe on Y
  // Probe on Y
  \_32位快速加法器  \u_32位快速加法器_1  (.X(X), .Y(Y), .C0(1'b0), .S(\n32位快速加法器_1_s ));  // open: C32, C31
  Divider #(.width(32)) divider_1 (.a(X), .b(Y), .out(divider_1_out), .rem(divider_1_rem));  // open: upper
  Multiplier #(.width(32)) multiplier_1 (.a(X), .b(Y), .out(multiplier_1_out), .cout(multiplier_1_cout));  // open: cin
  Shifter #(.width(32), .shift("lr")) shifter_1 (.in(X), .\dist (Y[4:0]), .out(shifter_1_out));
  Shifter #(.width(32), .shift("ar")) shifter_2 (.in(X), .\dist (Y[4:0]), .out(shifter_2_out));
  Shifter #(.width(32)) shifter_3 (.in(X), .\dist (Y[4:0]), .out(shifter_3_out));
  xor xor_2 (xor_2_out, \n32位快速加法器_2_c31 , \n32位快速加法器_2_c32 );
  \_32位快速加法器  \u_32位快速加法器_2  (.X(X), .Y(Y), .C32(\n32位快速加法器_2_c32 ), .C31(\n32位快速加法器_2_c31 ));  // open: C0, S
  Multiplexer #(.width(32), .enable("false")) multiplexer_1 (
    .in0({32{1'b0}}), .in1(32'h1), .out(multiplexer_1_out), .sel(comparator_1_lt));
  Multiplexer #(.width(32), .enable("false")) multiplexer_2 (
    .in0({32{1'b0}}), .in1(32'h1), .out(multiplexer_2_out), .sel(comparator_2_lt));
  Negator #(.width(32)) negator_1 (.in(Y), .out(negator_1_out));
  Negator #(.width(32)) negator_2 (.in(Y), .out(negator_2_out));
  Multiplexer #(.select(4), .enable("false")) multiplexer_3 (
    .in0(1'b0), .in1(1'b0), .in2(1'b0), .in3(1'b0), .in4(1'b0), .in5(xor_2_out), .in6(xor_3_out), .in7(1'b0),
    .in8(1'b0), .in9(1'b0), .in10(1'b0), .in11(1'b0), .in12(1'b0), .in13(1'b0), .in14(1'b0), .in15(1'b0),
    .out(Signed_Overflow), .sel(AluOP));
  // Probe on AluOP
  \_32位快速加法器  \u_32位快速加法器_3  (.X(X), .Y(negator_1_out), .C0(1'b0), .S(\n32位快速加法器_3_s ));  // open: C32, C31
  Multiplexer #(.select(4), .width(32), .enable("false")) multiplexer_4 (
    .in0(shifter_3_out), .in1(shifter_2_out), .in2(shifter_1_out), .in3(multiplier_1_out),
    .in4(divider_1_out), .in5(\n32位快速加法器_1_s ), .in6(\n32位快速加法器_3_s ), .in7(and_1_out), .in8(or_1_out),
    .in9(xor_1_out), .in10(nor_1_out), .in11(multiplexer_2_out), .in12(multiplexer_1_out), .in13({32{1'b0}}),
    .in14({32{1'b0}}), .in15({32{1'b0}}), .out(Result), .sel(AluOP));
  \_32位快速加法器  \u_32位快速加法器_4  (
    .X(X), .Y(negator_2_out), .C32(\n32位快速加法器_4_c32 ), .C31(\n32位快速加法器_4_c31 ));  // open: C0, S
  // Probe on Result
  // Probe on Result
  xor xor_3 (xor_3_out, \n32位快速加法器_4_c31 , \n32位快速加法器_4_c32 );
  \_32位快速加法器  \u_32位快速加法器_5  (.X(X), .Y(Y), .C32(\n32位快速加法器_5_c32 ));  // open: C0, S, C31
  // Probe on Result_2
  Negator #(.width(32)) negator_3 (.in(Y), .out(negator_3_out));
  Multiplexer #(.select(4), .width(32), .enable("false")) multiplexer_5 (
    .in0({32{1'b0}}), .in1({32{1'b0}}), .in2({32{1'b0}}), .in3(multiplier_1_cout), .in4(divider_1_rem),
    .in5({32{1'b0}}), .in6({32{1'b0}}), .in7({32{1'b0}}), .in8({32{1'b0}}), .in9({32{1'b0}}),
    .in10({32{1'b0}}), .in11({32{1'b0}}), .in12({32{1'b0}}), .in13({32{1'b0}}), .in14({32{1'b0}}),
    .in15({32{1'b0}}), .out(Result_2), .sel(AluOP));
  Multiplexer #(.select(4), .enable("false")) multiplexer_6 (
    .in0(1'b0), .in1(1'b0), .in2(1'b0), .in3(1'b0), .in4(1'b0), .in5(\n32位快速加法器_5_c32 ), .in6(not_1_out),
    .in7(1'b0), .in8(1'b0), .in9(1'b0), .in10(1'b0), .in11(1'b0), .in12(1'b0), .in13(1'b0), .in14(1'b0),
    .in15(1'b0), .out(UnSigned_Overflow), .sel(AluOP));
  not not_1 (not_1_out, \n32位快速加法器_6_c32 );
  \_32位快速加法器  \u_32位快速加法器_6  (.X(X), .Y(negator_3_out), .C32(\n32位快速加法器_6_c32 ));  // open: C0, S, C31

  // Other names for the same wires on the sheet: OF = Signed_Overflow; Result2[31:0] = Result_2; S[3:0] = AluOP;
  //   UOF = UnSigned_Overflow

  // Notes on the sheet:
  //   X: pull=down
  //   Y: pull=down
  //   AluOP: pull=down
  //   32位MIPS运算器
  //   32位MIPS运算器
  //   不要改变此引脚区域内容，也不要改变ALU封装形式
  //   输入引脚
  //   请在下方利用上方输入输出引脚的隧道信号构建ALU电路，ctrl+d复制选择部件
  //   华中科技大学计算机学院 计算机组成原理，鸣谢加州大学伯克利CS61C课程
  //   输出引脚
  //   探测区域
endmodule

module \ALU自动测试  (
  output [7:0] Test_num,
  output Equal
);

  wire ADD, AND, and_1_out, CF, CF_S, CLK, comparator_2_eq, comparator_3_eq, DIV, \EQ__标志 , EQ_OK, EQ_S,
       Halt, MUL, multiplexer_1_out, NEQ, nHalt, NOR, OF, OF_OK, OR, priority_encoder_1_gs, ROK, SAR, SCMP,
       SLL, SLR, SUB, tunnel, UCMP, UOF_OK, XOR, \与 , \乘法 , \减法 , \加法 , \异或 , \悬空检测 , \或 , \或非 , \无符号比较 ,
       \无符号溢出标志 , \有符号比较 , \有符号溢出标志 , \算术右移 , \逻辑右移 , \逻辑左移 , \除法 ;
  wire [2:2] FLAG_Standard;
  wire [3:0] ALUOP, High, Low, Mid;
  wire [7:0] adder_1_out, \单项评分_1_total , \单项评分_1_扣分 , \单项评分_1_正确条数 , \单项评分_2_total , \单项评分_2_扣分 ,
       \单项评分_2_正确条数 , \单项评分_3_total , \单项评分_3_扣分 , \单项评分_3_正确条数 , \单项评分_4_total , \单项评分_4_扣分 , \单项评分_4_正确条数 ,
       \单项评分_5_total , \单项评分_5_扣分 , \单项评分_5_正确条数 , \单项评分_6_total , \单项评分_6_扣分 , \单项评分_6_正确条数 ,
       \单项评分_7_total , \单项评分_7_扣分 , \单项评分_7_正确条数 , \单项评分_8_total , \单项评分_8_扣分 , \单项评分_8_正确条数 ,
       \单项评分_9_total , \单项评分_9_扣分 , \单项评分_9_正确条数 , \单项评分_10_total , \单项评分_10_扣分 , \单项评分_10_正确条数 ,
       \单项评分_11_total , \单项评分_11_扣分 , \单项评分_11_正确条数 , \单项评分_12_total , \单项评分_12_扣分 , \单项评分_12_正确条数 ,
       \单项评分_13_total , \单项评分_13_扣分 , \单项评分_13_正确条数 , \单项评分_14_total , \单项评分_14_扣分 , \单项评分_14_正确条数 ,
       \单项评分_15_total , \单项评分_15_扣分 , \单项评分_15_正确条数 , \单项评分_16_total , \单项评分_16_扣分 , \单项评分_16_正确条数 ,
       \总评分_result ;
  wire [9:0] counter_1_q;
  wire [31:0] bit_extender_1_out, R, R2, R2_Standard, R_Standard, X, Y;

  Clock clock_1 (.out(CLK));
  Register register_1 (.D(adder_1_out), .en(nHalt), .Q(Test_num), .clk(CLK));  // open: clr
  LED \u_测试完成  (.in(Halt));
  Counter #(.width(10), .max('h3ff)) counter_1 (
    .count(NEQ), .Q(counter_1_q), .clk(CLK), .clr(Halt));  // open: load, D, carry
  LED #(.active("false")) led_1 (.in(\逻辑左移 ));
  LED #(.active("false")) led_2 (.in(\逻辑右移 ));
  LED #(.active("false")) led_3 (.in(\EQ__标志 ));
  \单项评分  \u_单项评分_1  (
    .EQ(ROK), .EN(nHalt), .\分值 (5'b00101), .CLK(CLK), .\正确条数 (\单项评分_1_正确条数 ), .\扣分 (\单项评分_1_扣分 ),
    .Right(\逻辑左移 ), .ALU_SWITCH(SLL), .Total(\单项评分_1_total ));
  // Probe on \单项评分_1_total 
  // Probe on \单项评分_1_正确条数 
  // Probe on \单项评分_1_扣分 
  Adder adder_1 (.a(8'h1), .b(Test_num), .out(adder_1_out));  // open: cin, cout
  not not_1 (nHalt, Halt);
  Comparator #(.width(4)) comparator_1 (.a(ALUOP), .b(4'b1111), .eq(Halt));  // open: gt, lt
  and and_1 (and_1_out, ~Halt, NEQ);  // AND_Gate
  LED #(.active("false")) led_4 (.in(\算术右移 ));
  LED led_5 (.in(\悬空检测 ));
  \单项评分  \u_单项评分_2  (
    .EQ(ROK), .EN(nHalt), .\分值 (5'b00101), .CLK(CLK), .\正确条数 (\单项评分_2_正确条数 ), .\扣分 (\单项评分_2_扣分 ),
    .Right(\算术右移 ), .ALU_SWITCH(SAR), .Total(\单项评分_2_total ));
  // Probe on \单项评分_3_total 
  // Probe on \单项评分_2_total 
  // Probe on \单项评分_2_正确条数 
  // Probe on \单项评分_2_扣分 
  trace trace_1 (
    .in_1(Test_num), .X(X), .Y(Y), .AluOP(ALUOP), .R(R_Standard), .R2(R2_Standard),
    .FLAGS({FLAG_Standard[2], CF_S, EQ_S}));
  RAM #(.addrWidth(10), .dataWidth(32), .bus("separate")) ram_1 (
    .addr(counter_1_q), .din(X), .str(and_1_out), .clk(CLK));  // open: data, sel, ld, clr
  LED #(.active("false")) led_6 (.in(\与 ));
  LED #(.active("false")) led_7 (.in(\或 ));
  LED #(.active("false")) led_8 (.in(\有符号溢出标志 ));
  \单项评分  \u_单项评分_3  (
    .EQ(ROK), .EN(nHalt), .\分值 (5'b00101), .CLK(CLK), .\正确条数 (\单项评分_3_正确条数 ), .\扣分 (\单项评分_3_扣分 ),
    .Right(\逻辑右移 ), .ALU_SWITCH(SLR), .Total(\单项评分_3_total ));
  // Probe on \单项评分_4_total 
  // Probe on \单项评分_3_正确条数 
  // Probe on \单项评分_4_正确条数 
  // Probe on \单项评分_3_扣分 
  \单项评分  \u_单项评分_4  (
    .EQ(ROK), .EN(nHalt), .\分值 (5'b00101), .CLK(CLK), .\正确条数 (\单项评分_4_正确条数 ), .\扣分 (\单项评分_4_扣分 ),
    .Right(\乘法 ), .ALU_SWITCH(MUL), .Total(\单项评分_4_total ));
  // Probe on \单项评分_5_total 
  // Probe on \单项评分_5_正确条数 
  // Probe on \单项评分_4_扣分 
  // Probe on \单项评分_5_扣分 
  RAM #(.addrWidth(10), .dataWidth(32), .bus("separate")) ram_2 (
    .addr(counter_1_q), .din(Y), .str(and_1_out), .clk(CLK));  // open: data, sel, ld, clr
  assign bit_extender_1_out = {{28{1'b0}}, ALUOP};  // Bit_Extender bit_extender_1
  LED #(.active("false")) led_9 (.in(\或非 ));
  LED #(.active("false")) led_10 (.in(\异或 ));
  \单项评分  \u_单项评分_5  (
    .EQ(ROK), .EN(nHalt), .\分值 (5'b00101), .CLK(CLK), .\正确条数 (\单项评分_5_正确条数 ), .\扣分 (\单项评分_5_扣分 ),
    .Right(\除法 ), .ALU_SWITCH(DIV), .Total(\单项评分_5_total ));
  \单项评分  \u_单项评分_6  (
    .EQ(ROK), .EN(nHalt), .\分值 (5'b00101), .CLK(CLK), .\正确条数 (\单项评分_6_正确条数 ), .\扣分 (\单项评分_6_扣分 ),
    .Right(\加法 ), .ALU_SWITCH(ADD), .Total(\单项评分_6_total ));
  // Probe on \单项评分_6_total 
  // Probe on \单项评分_6_正确条数 
  // Probe on \单项评分_6_扣分 
  \算术逻辑运算单元ALU  \u_算术逻辑运算单元alu_1  (
    .AluOP(ALUOP), .X(X), .Equal(Equal), .Result(R), .Signed_Overflow(OF), .Y(Y), .Result_2(R2),
    .UnSigned_Overflow(CF));
  LED #(.active("false")) led_11 (.in(\乘法 ));
  LED #(.active("false")) led_12 (.in(\除法 ));
  LED #(.active("false")) led_13 (.in(\无符号溢出标志 ));
  \单项评分  \u_单项评分_7  (
    .EQ(ROK), .EN(nHalt), .\分值 (5'b00101), .CLK(CLK), .\正确条数 (\单项评分_7_正确条数 ), .\扣分 (\单项评分_7_扣分 ),
    .Right(\减法 ), .ALU_SWITCH(SUB), .Total(\单项评分_7_total ));
  // Probe on \单项评分_7_total 
  // Probe on \单项评分_7_正确条数 
  // Probe on \单项评分_7_扣分 
  RAM #(.addrWidth(10), .dataWidth(32), .bus("separate")) ram_3 (
    .addr(counter_1_q), .din(bit_extender_1_out), .str(and_1_out), .clk(CLK));  // open: data, sel, ld, clr
  LED #(.active("false")) led_14 (.in(\加法 ));
  LED #(.active("false")) led_15 (.in(\减法 ));
  \单项评分  \u_单项评分_8  (
    .EQ(ROK), .EN(nHalt), .\分值 (5'b00101), .CLK(CLK), .\正确条数 (\单项评分_8_正确条数 ), .\扣分 (\单项评分_8_扣分 ),
    .Right(\与 ), .ALU_SWITCH(AND), .Total(\单项评分_8_total ));
  // Probe on \单项评分_8_total 
  // Probe on \单项评分_8_正确条数 
  // Probe on \单项评分_8_扣分 
  \总评分  \u_总评分  (
    .in_1(\单项评分_1_扣分 ), .in_2(\单项评分_2_扣分 ), .in_3(\单项评分_3_扣分 ), .in_4(\单项评分_4_扣分 ), .in_5(\单项评分_5_扣分 ),
    .in_6(\单项评分_6_扣分 ), .in_7(\单项评分_7_扣分 ), .in_8(\单项评分_8_扣分 ), .in_9(\单项评分_9_扣分 ), .in_10(\单项评分_10_扣分 ),
    .in_11(\单项评分_11_扣分 ), .in_12(\单项评分_12_扣分 ), .in_13(\单项评分_13_扣分 ), .in_14(\单项评分_14_扣分 ),
    .in_15(\单项评分_15_扣分 ), .in_16(\单项评分_16_扣分 ), .\悬空扣分 (\悬空检测 ), .Result(\总评分_result ), .High(High),
    .Low(Low), .Mid(Mid));
  Hex_Digit_Display hex_digit_display_1 (.value(Mid));  // open: dp
  Hex_Digit_Display hex_digit_display_2 (.value(High));  // open: dp
  \单项评分  \u_单项评分_9  (
    .EQ(ROK), .EN(nHalt), .\分值 (5'b00101), .CLK(CLK), .\正确条数 (\单项评分_9_正确条数 ), .\扣分 (\单项评分_9_扣分 ),
    .Right(\或 ), .ALU_SWITCH(OR), .Total(\单项评分_9_total ));
  // Probe on nothing
  // Probe on \单项评分_9_正确条数 
  // Probe on \单项评分_9_扣分 
  // Probe on \总评分_result 
  Hex_Digit_Display hex_digit_display_3 (.value(Low));  // open: dp
  LED #(.active("false")) led_16 (.in(\有符号比较 ));
  LED #(.active("false")) led_17 (.in(\无符号比较 ));
  \单项评分  \u_单项评分_10  (
    .EQ(ROK), .EN(nHalt), .\分值 (5'b00101), .CLK(CLK), .\正确条数 (\单项评分_10_正确条数 ), .\扣分 (\单项评分_10_扣分 ),
    .Right(\异或 ), .ALU_SWITCH(XOR), .Total(\单项评分_10_total ));
  // Probe on \单项评分_10_total 
  // Probe on \单项评分_11_total 
  // Probe on \单项评分_10_正确条数 
  // Probe on \单项评分_10_扣分 
  \单项评分  \u_单项评分_11  (
    .EQ(ROK), .EN(nHalt), .\分值 (5'b00101), .CLK(CLK), .\正确条数 (\单项评分_11_正确条数 ), .\扣分 (\单项评分_11_扣分 ),
    .Right(\或非 ), .ALU_SWITCH(NOR), .Total(\单项评分_11_total ));
  // Probe on \单项评分_12_total 
  // Probe on \单项评分_11_正确条数 
  // Probe on \单项评分_12_正确条数 
  // Probe on \单项评分_11_扣分 
  \单项评分  \u_单项评分_12  (
    .EQ(ROK), .EN(nHalt), .\分值 (5'b00101), .CLK(CLK), .\正确条数 (\单项评分_12_正确条数 ), .\扣分 (\单项评分_12_扣分 ),
    .Right(\有符号比较 ), .ALU_SWITCH(SCMP), .Total(\单项评分_12_total ));
  // Probe on \单项评分_13_total 
  // Probe on \单项评分_13_正确条数 
  // Probe on \单项评分_13_扣分 
  // Probe on \单项评分_12_扣分 
  \单项评分  \u_单项评分_13  (
    .EQ(ROK), .EN(nHalt), .\分值 (5'b00101), .CLK(CLK), .\正确条数 (\单项评分_13_正确条数 ), .\扣分 (\单项评分_13_扣分 ),
    .Right(\无符号比较 ), .ALU_SWITCH(UCMP), .Total(\单项评分_13_total ));
  \单项评分  \u_单项评分_14  (
    .EQ(EQ_OK), .EN(nHalt), .\分值 (5'b01000), .CLK(CLK), .\正确条数 (\单项评分_14_正确条数 ), .\扣分 (\单项评分_14_扣分 ),
    .Right(\EQ__标志 ), .ALU_SWITCH(EQ_OK), .Total(\单项评分_14_total ));
  // Probe on \单项评分_14_total 
  // Probe on \单项评分_14_正确条数 
  // Probe on \单项评分_14_扣分 
  \单项评分  \u_单项评分_15  (
    .EQ(OF_OK), .EN(nHalt), .\分值 (5'b01000), .CLK(CLK), .\正确条数 (\单项评分_15_正确条数 ), .\扣分 (\单项评分_15_扣分 ),
    .Right(\有符号溢出标志 ), .ALU_SWITCH(1'b1), .Total(\单项评分_15_total ));
  // Probe on \单项评分_15_total 
  // Probe on \单项评分_15_正确条数 
  // Probe on \单项评分_15_扣分 
  \单项评分  \u_单项评分_16  (
    .EQ(UOF_OK), .EN(nHalt), .\分值 (5'b01000), .CLK(CLK), .\正确条数 (\单项评分_16_正确条数 ), .\扣分 (\单项评分_16_扣分 ),
    .Right(\无符号溢出标志 ), .ALU_SWITCH(1'b1), .Total(\单项评分_16_total ));
  // Probe on \单项评分_16_total 
  // Probe on \单项评分_16_正确条数 
  // Probe on \单项评分_16_扣分 
  // Probe on ALUOP
  Decoder #(.select(4), .enable("false")) decoder_1 (
    .out0(SLL), .out1(SAR), .out2(SLR), .out3(MUL), .out4(DIV), .out5(ADD), .out6(SUB), .out7(AND),
    .out8(OR), .out9(XOR), .out10(NOR), .out11(SCMP), .out12(UCMP), .sel(ALUOP));  // open: out13, out14, out15
  xnor xnor_1 (EQ_OK, EQ_S, Equal);
  xnor xnor_2 (OF_OK, FLAG_Standard[2], OF);
  xnor xnor_3 (UOF_OK, CF_S, CF);
  Comparator #(.width(32)) comparator_2 (.a(R_Standard), .b(R), .eq(comparator_2_eq));  // open: gt, lt
  Comparator #(.width(32)) comparator_3 (.a(R2_Standard), .b(R2), .eq(comparator_3_eq));  // open: gt, lt
  Multiplexer #(.disabled(0), .enable("false")) multiplexer_1 (
    .in0(1'b1), .in1(1'b1), .out(multiplexer_1_out), .sel(CF));
  and and_2 (ROK, comparator_2_eq, comparator_3_eq);
  or or_1 (tunnel, ADD, SUB);
  Priority_Encoder #(.select(1)) priority_encoder_1 (
    .in0(multiplexer_1_out), .in1(multiplexer_1_out), .gs(priority_encoder_1_gs));  // open: out, en_out, en_in
  not not_2 (\悬空检测 , priority_encoder_1_gs);
  nand nand_1 (NEQ, EQ_OK, OF_OK, UOF_OK, ROK);

  // Other names for the same wires on the sheet: EQ = Equal; FLAG_Standard[1:0] = {CF_S, EQ_S};
  //   OF_S = FLAG_Standard[2]

  // Notes on the sheet:
  //   操作码为F停止
  //   错误记录X
  //   错误记录Y
  //   运算故障指示灯，红色异常
  //   错误记录ALUOP
  //   3个存储器存储的是所有错误的测试用例
  //   错误扣分值
  //   成绩
  //   ctrl+K驱动时钟自动测试
  //   华中科技大学：计算机组成课程组
  //   悬空扣5分
  //   错误扣分值
  //   各部分分值
  //   各部分扣分
  //   悬空检测
endmodule

// 与门阵列
module \_5位乘法与门阵列  (
  input  [4:0] X,
  input  [4:0] Y,
  output [4:0] XY0,
  output [4:0] XY1,
  output [4:0] XY2,
  output [4:0] XY3,
  output [4:0] XY4
);

  and and_1 (XY0[4], X[4], Y[0]);
  and and_2 (XY1[4], X[4], Y[1]);
  and and_3 (XY2[4], X[4], Y[2]);
  and and_4 (XY3[4], X[4], Y[3]);
  and and_5 (XY4[4], X[4], Y[4]);
  and and_6 (XY0[3], X[3], Y[0]);
  and and_7 (XY1[3], X[3], Y[1]);
  and and_8 (XY2[3], X[3], Y[2]);
  and and_9 (XY3[3], X[3], Y[3]);
  and and_10 (XY4[3], X[3], Y[4]);
  and and_11 (XY0[2], X[2], Y[0]);
  and and_12 (XY1[2], X[2], Y[1]);
  and and_13 (XY2[2], X[2], Y[2]);
  and and_14 (XY3[2], X[2], Y[3]);
  and and_15 (XY4[2], X[2], Y[4]);
  and and_16 (XY0[0], X[0], Y[0]);
  and and_17 (XY0[1], X[1], Y[0]);
  and and_18 (XY1[0], X[0], Y[1]);
  and and_19 (XY1[1], X[1], Y[1]);
  and and_20 (XY2[1], X[1], Y[2]);
  and and_21 (XY2[0], X[0], Y[2]);
  and and_22 (XY3[1], X[1], Y[3]);
  and and_23 (XY3[0], X[0], Y[3]);
  and and_24 (XY4[1], X[1], Y[4]);
  and and_25 (XY4[0], X[0], Y[4]);

  // Other names for the same wires on the sheet: X0Y0 = XY0[0]; X1Y0 = XY0[1]; X2Y0 = XY0[2]; X3Y0 = XY0[3];
  //   X4Y0 = XY0[4]; X0Y1 = XY1[0]; X1Y1 = XY1[1]; X2Y1 = XY1[2]; X3Y1 = XY1[3]; X4Y1 = XY1[4]; X0Y2 = XY2[0];
  //   X1Y2 = XY2[1]; X2Y2 = XY2[2]; X3Y2 = XY2[3]; X4Y2 = XY2[4]; X0Y3 = XY3[0]; X1Y3 = XY3[1]; X2Y3 = XY3[2];
  //   X3Y3 = XY3[3]; X4Y3 = XY3[4]; X0Y4 = XY4[0]; X1Y4 = XY4[1]; X2Y4 = XY4[2]; X3Y4 = XY4[3]; X4Y4 = XY4[4]
endmodule

module \乘法线流水接口  (
  input  [4:0] X,
  input  [4:0] Y,
  input  [4:0] XY0,
  input  [4:0] XY1,
  input  [4:0] XY2,
  input  [4:0] XY3,
  input  [4:0] XY4,
  input  [9:0] in_8,
  input  CLK,
  input  \同步清零_高电平有效 ,
  input  \使能端_低电平有效 ,
  output [4:0] X_prime,
  output [4:0] Y_prime,
  output [4:0] XY0_prime,
  output [4:0] XY1_prime,
  output [4:0] XY2_prime,
  output [4:0] XY3_2,
  output [4:0] XY4_2,
  output [9:0] out_19,
  output [9:0] EDU
);

  wire pull_resistor_2_node;
  wire [4:0] multiplexer_1_out, multiplexer_2_out, multiplexer_3_out, multiplexer_4_out, multiplexer_5_out,
       multiplexer_6_out, multiplexer_7_out;
  wire [9:0] multiplexer_8_out;

  Multiplexer #(.width(5), .enable("false")) multiplexer_1 (
    .in0(X), .in1({5{1'b0}}), .out(multiplexer_1_out), .sel(\同步清零_高电平有效 ));
  Multiplexer #(.width(5), .enable("false")) multiplexer_2 (
    .in0(Y), .in1({5{1'b0}}), .out(multiplexer_2_out), .sel(\同步清零_高电平有效 ));
  Multiplexer #(.width(5), .enable("false")) multiplexer_3 (
    .in0(XY0), .in1({5{1'b0}}), .out(multiplexer_3_out), .sel(\同步清零_高电平有效 ));
  Multiplexer #(.width(5), .enable("false")) multiplexer_4 (
    .in0(XY1), .in1({5{1'b0}}), .out(multiplexer_4_out), .sel(\同步清零_高电平有效 ));
  Multiplexer #(.width(5), .enable("false")) multiplexer_5 (
    .in0(XY2), .in1({5{1'b0}}), .out(multiplexer_5_out), .sel(\同步清零_高电平有效 ));
  Multiplexer #(.width(5), .enable("false")) multiplexer_6 (
    .in0(XY3), .in1({5{1'b0}}), .out(multiplexer_6_out), .sel(\同步清零_高电平有效 ));
  Multiplexer #(.width(5), .enable("false")) multiplexer_7 (
    .in0(XY4), .in1({5{1'b0}}), .out(multiplexer_7_out), .sel(\同步清零_高电平有效 ));
  Multiplexer #(.width(10), .enable("false")) multiplexer_8 (
    .in0(in_8), .in1({10{1'b0}}), .out(multiplexer_8_out), .sel(\同步清零_高电平有效 ));
  Pull_Resistor pull_resistor_1 (.node(\同步清零_高电平有效 ));
  Register #(.width(5)) register_1 (
    .D(multiplexer_1_out), .en(pull_resistor_2_node), .Q(X_prime), .clk(CLK));  // open: clr
  Register #(.width(5)) register_2 (
    .D(multiplexer_2_out), .en(pull_resistor_2_node), .Q(Y_prime), .clk(CLK));  // open: clr
  Register #(.width(5)) register_3 (
    .D(multiplexer_3_out), .en(pull_resistor_2_node), .Q(XY0_prime), .clk(CLK));  // open: clr
  Register #(.width(5)) register_4 (
    .D(multiplexer_4_out), .en(pull_resistor_2_node), .Q(XY1_prime), .clk(CLK));  // open: clr
  Register #(.width(5)) register_5 (
    .D(multiplexer_5_out), .en(pull_resistor_2_node), .Q(XY2_prime), .clk(CLK));  // open: clr
  Register #(.width(5)) register_6 (
    .D(multiplexer_6_out), .en(pull_resistor_2_node), .Q(XY3_2), .clk(CLK));  // open: clr
  Register #(.width(5)) register_7 (
    .D(multiplexer_7_out), .en(pull_resistor_2_node), .Q(XY4_2), .clk(CLK));  // open: clr
  Register #(.width(10)) register_8 (
    .D(multiplexer_8_out), .en(pull_resistor_2_node), .Q(EDU), .clk(CLK));  // open: clr
  Pull_Resistor pull_resistor_2 (.node(pull_resistor_2_node));
  not not_1 (pull_resistor_2_node, \使能端_低电平有效 );

  assign out_19 = EDU;

  // Notes on the sheet:
  //   使能端_低电平有效: pull=down
  //   同步清零_高电平有效: pull=down
  //   下拉电阻使得引脚可以悬空
  //   流水接口传输XY的目的是为了测试
endmodule

// FA
module \一位全加器FA封装1  (
  input  Cin,
  input  Xi,
  input  Yi,
  output Cout,
  output Si
);

  wire AND_2_out, AND_out, XOR_2_out;

  or OR (Cout, AND_out, AND_2_out);
  and AND (AND_out, Xi, Yi);
  and AND_2 (AND_2_out, Cin, XOR_2_out);
  xor XOR (Si, Cin, XOR_2_out);
  xor XOR_2 (XOR_2_out, Xi, Yi);

  // Notes on the sheet:
  //   Yi: pull=down
  //   Cin: pull=down
  //   Xi: pull=down
  //   Si = Xi ^ Yi ^ Cin
  //   Cout = Xi Yi + Cin (Xi ^ Yi)
endmodule

module \一位全加器FA封装2  (
  input  Cin,
  input  Xi,
  input  Yi,
  output Cout,
  output Si
);

  wire AND_2_out, AND_out, XOR_2_out;

  or OR (Cout, AND_out, AND_2_out);
  and AND (AND_out, Xi, Yi);
  and AND_2 (AND_2_out, Cin, XOR_2_out);
  xor XOR (Si, Cin, XOR_2_out);
  xor XOR_2 (XOR_2_out, Xi, Yi);

  // Notes on the sheet:
  //   Yi: pull=down
  //   Xi: pull=down
  //   Cin: pull=down
  //   Si = Xi ^ Yi ^ Cin
  //   Cout = Xi Yi + Cin (Xi ^ Yi)
endmodule

module \一位全加器FA封装3  (
  input  Cin,
  input  Xi,
  input  Yi,
  output Cout,
  output Si
);

  wire AND_2_out, AND_out, XOR_2_out;

  or OR (Cout, AND_out, AND_2_out);
  and AND (AND_out, Xi, Yi);
  and AND_2 (AND_2_out, Cin, XOR_2_out);
  xor XOR (Si, Cin, XOR_2_out);
  xor XOR_2 (XOR_2_out, Xi, Yi);

  // Notes on the sheet:
  //   Si = Xi ^ Yi ^ Cin
  //   Cout = Xi Yi + Cin (Xi ^ Yi)
endmodule

module \_8位串行加法器  (
  input  [7:0] X,
  input  [7:0] Y,
  input  Cin,
  output [7:0] S,
  output Cout,
  output Overflow
);

  wire \一位全加器fa封装1_2_cout , \一位全加器fa封装1_3_cout , \一位全加器fa封装1_4_cout , \一位全加器fa封装1_5_cout ,
       \一位全加器fa封装1_6_cout , \一位全加器fa封装1_7_cout , \一位全加器fa封装1_8_cout ;

  xor xor_1 (Overflow, Cout, \一位全加器fa封装1_2_cout );
  \一位全加器FA封装1  \u_一位全加器fa封装1_1  (.Cout(Cout), .Si(S[7]), .Cin(X[7]), .Xi(\一位全加器fa封装1_2_cout ), .Yi(Y[7]));
  \一位全加器FA封装1  \u_一位全加器fa封装1_2  (
    .Cout(\一位全加器fa封装1_2_cout ), .Si(S[6]), .Cin(X[6]), .Xi(\一位全加器fa封装1_3_cout ), .Yi(Y[6]));
  \一位全加器FA封装1  \u_一位全加器fa封装1_3  (
    .Cout(\一位全加器fa封装1_3_cout ), .Si(S[5]), .Cin(X[5]), .Xi(\一位全加器fa封装1_4_cout ), .Yi(Y[5]));
  \一位全加器FA封装1  \u_一位全加器fa封装1_4  (
    .Cout(\一位全加器fa封装1_4_cout ), .Si(S[4]), .Cin(X[4]), .Xi(\一位全加器fa封装1_5_cout ), .Yi(Y[4]));
  \一位全加器FA封装1  \u_一位全加器fa封装1_5  (
    .Cout(\一位全加器fa封装1_5_cout ), .Si(S[3]), .Cin(X[3]), .Xi(\一位全加器fa封装1_6_cout ), .Yi(Y[3]));
  \一位全加器FA封装1  \u_一位全加器fa封装1_6  (
    .Cout(\一位全加器fa封装1_6_cout ), .Si(S[2]), .Cin(X[2]), .Xi(\一位全加器fa封装1_7_cout ), .Yi(Y[2]));
  // Probe on X
  // Probe on Y
  // Probe on S
  \一位全加器FA封装1  \u_一位全加器fa封装1_7  (
    .Cout(\一位全加器fa封装1_7_cout ), .Si(S[1]), .Cin(X[1]), .Xi(\一位全加器fa封装1_8_cout ), .Yi(Y[1]));
  // Probe on X
  // Probe on Y
  // Probe on S
  \一位全加器FA封装1  \u_一位全加器fa封装1_8  (.Cout(\一位全加器fa封装1_8_cout ), .Si(S[0]), .Cin(X[0]), .Xi(Cin), .Yi(Y[0]));

  // Other names for the same wires on the sheet: OF = Overflow

  // Notes on the sheet:
  //   X: pull=down
  //   Y: pull=down
  //   Cin: pull=down
  //   输入引脚区
  //   符号位
  //   输出引脚区
  //   +
  //   =
  //   有符号加法
  //   +
  //   =
  //   无符号加法
endmodule

module \华莱士树  (
);

  wire \一位全加器fa封装2_1_p1 , \一位全加器fa封装2_1_p2 , \一位全加器fa封装2_1_p3 , \一位全加器fa封装2_1_p4 , \一位全加器fa封装2_1_p5 ,
       \一位全加器fa封装2_2_p3 , \一位全加器fa封装2_2_p4 , \一位全加器fa封装2_2_p6 , \一位全加器fa封装2_3_p1 , \一位全加器fa封装2_3_p2 ,
       \一位全加器fa封装2_3_p4 , \一位全加器fa封装2_4_p3 , \一位全加器fa封装2_4_p5 , \一位全加器fa封装2_6_p3 , \一位全加器fa封装2_6_p4 ,
       \一位全加器fa封装2_6_p6 , \一位全加器fa封装2_7_p3 , \一位全加器fa封装2_7_p4 , \一位全加器fa封装2_8_p2 , \一位全加器fa封装2_8_p3 ,
       \一位全加器fa封装2_8_p4 , \一位全加器fa封装2_8_p5 , \一位全加器fa封装2_9_p1 , \一位全加器fa封装2_9_p2 , \一位全加器fa封装2_9_p4 ,
       \一位全加器fa封装2_10_p2 , \一位全加器fa封装2_10_p3 , \一位全加器fa封装2_10_p5 , \一位全加器fa封装2_12_p3 , \一位全加器fa封装2_12_p5 ,
       \一位全加器fa封装2_13_p3 , \一位全加器fa封装2_13_p4 , \一位全加器fa封装2_13_p6 , \一位全加器fa封装2_14_p3 , \一位全加器fa封装2_14_p4 ,
       \一位全加器fa封装2_15_p1 , \一位全加器fa封装2_15_p2 , \一位全加器fa封装2_15_p4 , \一位全加器fa封装2_16_p2 , \一位全加器fa封装2_16_p3 ,
       \一位全加器fa封装2_16_p5 , \一位全加器fa封装2_17_p2 , \一位全加器fa封装2_17_p3 , \一位全加器fa封装2_17_p5 , \一位全加器fa封装2_18_p2 ,
       \一位全加器fa封装2_18_p3 , \一位全加器fa封装2_18_p5 , \一位全加器fa封装2_19_p3 , \一位全加器fa封装2_19_p4 , \一位全加器fa封装2_19_p6 ,
       \一位全加器fa封装2_21_p3 , \一位全加器fa封装2_21_p4 , \一位全加器fa封装2_22_p2 , \一位全加器fa封装2_22_p3 , \一位全加器fa封装2_22_p4 ,
       \一位全加器fa封装2_22_p5 , \一位全加器fa封装2_23_p2 , \一位全加器fa封装2_23_p3 , \一位全加器fa封装2_23_p5 , \一位全加器fa封装2_24_p2 ,
       \一位全加器fa封装2_24_p3 , \一位全加器fa封装2_24_p5 , \一位全加器fa封装2_25_p1 , \一位全加器fa封装2_25_p4 , \一位全加器fa封装2_27_p3 ,
       \一位全加器fa封装2_27_p4 , \一位全加器fa封装2_28_p3 , \一位全加器fa封装2_28_p4 , \一位全加器fa封装2_28_p6 , \一位全加器fa封装2_29_p2 ,
       \一位全加器fa封装2_29_p3 , \一位全加器fa封装2_29_p4 , \一位全加器fa封装2_29_p5 , \一位全加器fa封装2_30_p2 , \一位全加器fa封装2_30_p3 ,
       \一位全加器fa封装2_30_p5 , \一位全加器fa封装2_31_p1 , \一位全加器fa封装2_31_p2 , \一位全加器fa封装2_31_p4 , \一位全加器fa封装2_32_p3 ,
       \一位全加器fa封装2_32_p5 , \一位全加器fa封装2_34_p3 , \一位全加器fa封装2_34_p4 , \一位全加器fa封装2_34_p6 , \一位全加器fa封装2_35_p3 ,
       \一位全加器fa封装2_35_p4 , \一位全加器fa封装2_36_p2 , \一位全加器fa封装2_36_p3 , \一位全加器fa封装2_36_p4 , \一位全加器fa封装2_36_p5 ,
       \一位全加器fa封装2_37_p1 , \一位全加器fa封装2_37_p2 , \一位全加器fa封装2_37_p4 , \一位全加器fa封装2_38_p2 , \一位全加器fa封装2_38_p3 ,
       \一位全加器fa封装2_38_p5 , \一位全加器fa封装2_40_p3 , \一位全加器fa封装2_40_p5 , \一位全加器fa封装2_41_p3 , \一位全加器fa封装2_41_p4 ,
       \一位全加器fa封装2_41_p6 , \一位全加器fa封装2_42_p3 , \一位全加器fa封装2_42_p4 , \一位全加器fa封装2_43_p1 , \一位全加器fa封装2_43_p2 ,
       \一位全加器fa封装2_43_p4 , \一位全加器fa封装2_44_p2 , \一位全加器fa封装2_44_p3 , \一位全加器fa封装2_44_p5 , \一位全加器fa封装2_45_p2 ,
       \一位全加器fa封装2_45_p3 , \一位全加器fa封装2_45_p5 , \一位全加器fa封装2_46_p3 , \一位全加器fa封装2_46_p4 , \一位全加器fa封装2_46_p6 ,
       \一位全加器fa封装2_47_p2 , \一位全加器fa封装2_47_p3 , \一位全加器fa封装2_47_p5 , \一位全加器fa封装2_49_p3 , \一位全加器fa封装2_49_p4 ,
       \一位全加器fa封装2_50_p2 , \一位全加器fa封装2_50_p3 , \一位全加器fa封装2_50_p4 , \一位全加器fa封装2_50_p5 , \一位全加器fa封装2_51_p2 ,
       \一位全加器fa封装2_51_p3 , \一位全加器fa封装2_51_p5 , \一位全加器fa封装2_52_p2 , \一位全加器fa封装2_52_p3 , \一位全加器fa封装2_52_p5 ,
       \一位全加器fa封装2_53_p1 , \一位全加器fa封装2_53_p4 , \一位全加器fa封装2_55_p3 , \一位全加器fa封装2_55_p4 , \一位全加器fa封装2_55_p6 ,
       \一位全加器fa封装2_56_p3 , \一位全加器fa封装2_56_p4 , \一位全加器fa封装2_57_p2 , \一位全加器fa封装2_57_p3 , \一位全加器fa封装2_57_p4 ,
       \一位全加器fa封装2_57_p5 , \一位全加器fa封装2_58_p2 , \一位全加器fa封装2_58_p3 , \一位全加器fa封装2_58_p5 , \一位全加器fa封装2_59_p1 ,
       \一位全加器fa封装2_59_p2 , \一位全加器fa封装2_59_p4 , \一位全加器fa封装2_60_p3 , \一位全加器fa封装2_60_p5 , \一位全加器fa封装2_62_p3 ,
       \一位全加器fa封装2_62_p4 , \一位全加器fa封装2_63_p3 , \一位全加器fa封装2_63_p4 , \一位全加器fa封装2_63_p6 , \一位全加器fa封装2_64_p2 ,
       \一位全加器fa封装2_64_p3 , \一位全加器fa封装2_64_p4 , \一位全加器fa封装2_64_p5 , \一位全加器fa封装2_65_p1 , \一位全加器fa封装2_65_p2 ,
       \一位全加器fa封装2_65_p4 , \一位全加器fa封装2_66_p2 , \一位全加器fa封装2_66_p3 , \一位全加器fa封装2_66_p5 , \一位全加器fa封装2_68_p3 ,
       \一位全加器fa封装2_68_p5 , \一位全加器fa封装2_69_p3 , \一位全加器fa封装2_69_p4 , \一位全加器fa封装2_69_p6 , \一位全加器fa封装2_70_p3 ,
       \一位全加器fa封装2_70_p4 , \一位全加器fa封装2_71_p1 , \一位全加器fa封装2_71_p2 , \一位全加器fa封装2_71_p4 , \一位全加器fa封装2_72_p2 ,
       \一位全加器fa封装2_72_p3 , \一位全加器fa封装2_72_p5 , \一位全加器fa封装2_73_p2 , \一位全加器fa封装2_73_p3 , \一位全加器fa封装2_73_p5 ,
       \一位全加器fa封装2_74_p3 , \一位全加器fa封装2_74_p4 , \一位全加器fa封装2_74_p6 , \一位全加器fa封装2_75_p2 , \一位全加器fa封装2_75_p3 ,
       \一位全加器fa封装2_75_p5 , \一位全加器fa封装2_77_p3 , \一位全加器fa封装2_77_p4 , \一位全加器fa封装2_78_p2 , \一位全加器fa封装2_78_p3 ,
       \一位全加器fa封装2_78_p4 , \一位全加器fa封装2_78_p5 , \一位全加器fa封装2_79_p2 , \一位全加器fa封装2_79_p3 , \一位全加器fa封装2_79_p5 ,
       \一位全加器fa封装2_80_p2 , \一位全加器fa封装2_80_p3 , \一位全加器fa封装2_80_p5 , \一位全加器fa封装2_81_p1 , \一位全加器fa封装2_81_p4 ,
       \一位全加器fa封装2_83_p3 , \一位全加器fa封装2_83_p4 , \一位全加器fa封装2_83_p6 , \一位全加器fa封装2_84_p3 , \一位全加器fa封装2_84_p4 ,
       \一位全加器fa封装2_85_p2 , \一位全加器fa封装2_85_p3 , \一位全加器fa封装2_85_p4 , \一位全加器fa封装2_85_p5 , \一位全加器fa封装2_86_p2 ,
       \一位全加器fa封装2_86_p3 , \一位全加器fa封装2_86_p5 , \一位全加器fa封装2_87_p1 , \一位全加器fa封装2_87_p2 , \一位全加器fa封装2_87_p4 ,
       \一位全加器fa封装2_88_p3 , \一位全加器fa封装2_88_p5 , \一位全加器fa封装2_90_p3 , \一位全加器fa封装2_90_p4 , \一位全加器fa封装2_90_p6 ,
       \一位全加器fa封装2_91_p3 , \一位全加器fa封装2_91_p4 , \一位全加器fa封装2_92_p2 , \一位全加器fa封装2_92_p3 , \一位全加器fa封装2_92_p4 ,
       \一位全加器fa封装2_92_p5 , \一位全加器fa封装2_93_p1 , \一位全加器fa封装2_93_p2 , \一位全加器fa封装2_93_p4 , \一位全加器fa封装2_94_p2 ,
       \一位全加器fa封装2_94_p3 , \一位全加器fa封装2_94_p5 , \一位全加器fa封装2_96_p3 , \一位全加器fa封装2_96_p5 , \一位全加器fa封装2_97_p3 ,
       \一位全加器fa封装2_97_p4 , \一位全加器fa封装2_97_p6 , \一位全加器fa封装2_98_p3 , \一位全加器fa封装2_98_p4 , \一位全加器fa封装2_99_p1 ,
       \一位全加器fa封装2_99_p2 , \一位全加器fa封装2_99_p4 , \一位全加器fa封装2_100_p2 , \一位全加器fa封装2_100_p3 , \一位全加器fa封装2_100_p5 ,
       \一位全加器fa封装2_101_p2 , \一位全加器fa封装2_101_p3 , \一位全加器fa封装2_101_p5 , \一位全加器fa封装2_102_p2 ,
       \一位全加器fa封装2_102_p3 , \一位全加器fa封装2_102_p5 , \一位全加器fa封装2_103_p3 , \一位全加器fa封装2_103_p4 ,
       \一位全加器fa封装2_103_p6 , \一位全加器fa封装2_105_p3 , \一位全加器fa封装2_105_p4 , \一位全加器fa封装2_106_p2 ,
       \一位全加器fa封装2_106_p3 , \一位全加器fa封装2_106_p4 , \一位全加器fa封装2_106_p5 , \一位全加器fa封装2_107_p2 ,
       \一位全加器fa封装2_107_p3 , \一位全加器fa封装2_107_p5 , \一位全加器fa封装2_108_p2 , \一位全加器fa封装2_108_p3 ,
       \一位全加器fa封装2_108_p5 , \一位全加器fa封装2_109_p1 , \一位全加器fa封装2_109_p4 , \一位全加器fa封装2_111_p3 ,
       \一位全加器fa封装2_111_p4 , \一位全加器fa封装2_112_p3 , \一位全加器fa封装2_112_p4 , \一位全加器fa封装2_112_p6 ;
  wire [1:0] \一位全加器fa封装2_3_p5 , \一位全加器fa封装2_4_p1 , \一位全加器fa封装2_9_p5 , \一位全加器fa封装2_15_p5 , \一位全加器fa封装2_25_p5 ,
       \一位全加器fa封装2_31_p5 , \一位全加器fa封装2_37_p5 , \一位全加器fa封装2_43_p5 , \一位全加器fa封装2_53_p5 , \一位全加器fa封装2_59_p5 ,
       \一位全加器fa封装2_65_p5 , \一位全加器fa封装2_71_p5 , \一位全加器fa封装2_81_p5 , \一位全加器fa封装2_87_p5 , \一位全加器fa封装2_93_p5 ,
       \一位全加器fa封装2_99_p5 , \一位全加器fa封装2_109_p5 ;
  wire [2:0] \一位全加器fa封装2_2_p1 , \一位全加器fa封装2_5_p5 , \一位全加器fa封装2_11_p5 , \一位全加器fa封装2_20_p5 ,
       \一位全加器fa封装2_26_p5 , \一位全加器fa封装2_33_p5 , \一位全加器fa封装2_39_p5 , \一位全加器fa封装2_48_p5 , \一位全加器fa封装2_54_p5 ,
       \一位全加器fa封装2_61_p5 , \一位全加器fa封装2_67_p5 , \一位全加器fa封装2_76_p5 , \一位全加器fa封装2_82_p5 , \一位全加器fa封装2_89_p5 ,
       \一位全加器fa封装2_95_p5 , \一位全加器fa封装2_104_p5 , \一位全加器fa封装2_110_p5 ;

  shape shape_1 ();
  // 一位全加器FA封装2 一位全加器fa封装2_1: pin names not known; wires that end beside it: \一位全加器fa封装2_1_p1 , \一位全加器fa封装2_1_p2 , \一位全加器fa封装2_1_p3 , \一位全加器fa封装2_1_p4 , \一位全加器fa封装2_1_p5 
  // 一位全加器FA封装2 一位全加器fa封装2_2: pin names not known; wires that end beside it: \一位全加器fa封装2_2_p1 , \一位全加器fa封装2_2_p1 [2], \一位全加器fa封装2_2_p3 , \一位全加器fa封装2_2_p4 , \一位全加器fa封装2_1_p2 , \一位全加器fa封装2_2_p6 
  // 一位全加器FA封装2 一位全加器fa封装2_3: pin names not known; wires that end beside it: \一位全加器fa封装2_3_p1 , \一位全加器fa封装2_3_p2 , \一位全加器fa封装2_3_p5 [1], \一位全加器fa封装2_3_p4 , \一位全加器fa封装2_3_p5 [0]
  // 一位全加器FA封装2 一位全加器fa封装2_4: pin names not known; wires that end beside it: \一位全加器fa封装2_4_p1 [0], \一位全加器fa封装2_1_p4 , \一位全加器fa封装2_4_p3 , \一位全加器fa封装2_3_p2 , \一位全加器fa封装2_4_p5 
  // 一位全加器FA封装2 一位全加器fa封装2_5: pin names not known; wires that end beside it: \一位全加器fa封装2_4_p1 [1], \一位全加器fa封装2_5_p5 [2], \一位全加器fa封装2_5_p5 [1], \一位全加器fa封装2_4_p3 , \一位全加器fa封装2_5_p5 [0]
  // 一位全加器FA封装2 一位全加器fa封装2_6: pin names not known; wires that end beside it: \一位全加器fa封装2_1_p2 , \一位全加器fa封装2_2_p1 [1], \一位全加器fa封装2_6_p3 , \一位全加器fa封装2_6_p4 , \一位全加器fa封装2_1_p3 , \一位全加器fa封装2_6_p6 
  // 一位全加器FA封装2 一位全加器fa封装2_7: pin names not known; wires that end beside it: \一位全加器fa封装2_1_p3 , \一位全加器fa封装2_2_p1 [0], \一位全加器fa封装2_7_p3 , \一位全加器fa封装2_7_p4 , \一位全加器fa封装2_1_p5 , 1'b0
  // 一位全加器FA封装2 一位全加器fa封装2_8: pin names not known; wires that end beside it: \一位全加器fa封装2_5_p5 [2], \一位全加器fa封装2_8_p2 , \一位全加器fa封装2_8_p3 , \一位全加器fa封装2_8_p4 , \一位全加器fa封装2_8_p5 
  // 一位全加器FA封装2 一位全加器fa封装2_9: pin names not known; wires that end beside it: \一位全加器fa封装2_9_p1 , \一位全加器fa封装2_9_p2 , \一位全加器fa封装2_9_p5 [1], \一位全加器fa封装2_9_p4 , \一位全加器fa封装2_9_p5 [0]
  // 一位全加器FA封装2 一位全加器fa封装2_10: pin names not known; wires that end beside it: \一位全加器fa封装2_3_p5 [0], \一位全加器fa封装2_10_p2 , \一位全加器fa封装2_10_p3 , \一位全加器fa封装2_9_p2 , \一位全加器fa封装2_10_p5 
  // 一位全加器FA封装2 一位全加器fa封装2_11: pin names not known; wires that end beside it: \一位全加器fa封装2_3_p5 [1], \一位全加器fa封装2_11_p5 [2], \一位全加器fa封装2_11_p5 [1], \一位全加器fa封装2_10_p3 , \一位全加器fa封装2_11_p5 [0]
  // 一位全加器FA封装2 一位全加器fa封装2_12: pin names not known; wires that end beside it: \一位全加器fa封装2_4_p5 , \一位全加器fa封装2_8_p4 , \一位全加器fa封装2_12_p3 , \一位全加器fa封装2_10_p2 , \一位全加器fa封装2_12_p5 
  // 一位全加器FA封装2 一位全加器fa封装2_13: pin names not known; wires that end beside it: \一位全加器fa封装2_8_p4 , \一位全加器fa封装2_5_p5 [1], \一位全加器fa封装2_13_p3 , \一位全加器fa封装2_13_p4 , \一位全加器fa封装2_12_p3 , \一位全加器fa封装2_13_p6 
  shape shape_2 ();
  // 一位全加器FA封装2 一位全加器fa封装2_14: pin names not known; wires that end beside it: \一位全加器fa封装2_12_p3 , \一位全加器fa封装2_5_p5 [0], \一位全加器fa封装2_14_p3 , \一位全加器fa封装2_14_p4 , \一位全加器fa封装2_12_p5 , 1'b0
  // 一位全加器FA封装2 一位全加器fa封装2_15: pin names not known; wires that end beside it: \一位全加器fa封装2_15_p1 , \一位全加器fa封装2_15_p2 , \一位全加器fa封装2_15_p5 [1], \一位全加器fa封装2_15_p4 , \一位全加器fa封装2_15_p5 [0]
  // 一位全加器FA封装2 一位全加器fa封装2_16: pin names not known; wires that end beside it: \一位全加器fa封装2_9_p5 [0], \一位全加器fa封装2_16_p2 , \一位全加器fa封装2_16_p3 , \一位全加器fa封装2_15_p2 , \一位全加器fa封装2_16_p5 
  // 一位全加器FA封装2 一位全加器fa封装2_17: pin names not known; wires that end beside it: \一位全加器fa封装2_10_p5 , \一位全加器fa封装2_17_p2 , \一位全加器fa封装2_17_p3 , \一位全加器fa封装2_16_p2 , \一位全加器fa封装2_17_p5 
  // 一位全加器FA封装2 一位全加器fa封装2_18: pin names not known; wires that end beside it: \一位全加器fa封装2_11_p5 [2], \一位全加器fa封装2_18_p2 , \一位全加器fa封装2_18_p3 , \一位全加器fa封装2_17_p2 , \一位全加器fa封装2_18_p5 
  // 一位全加器FA封装2 一位全加器fa封装2_19: pin names not known; wires that end beside it: \一位全加器fa封装2_17_p2 , \一位全加器fa封装2_11_p5 [1], \一位全加器fa封装2_19_p3 , \一位全加器fa封装2_19_p4 , \一位全加器fa封装2_17_p3 , \一位全加器fa封装2_19_p6 
  // 一位全加器FA封装2 一位全加器fa封装2_20: pin names not known; wires that end beside it: \一位全加器fa封装2_9_p5 [1], \一位全加器fa封装2_20_p5 [2], \一位全加器fa封装2_20_p5 [1], \一位全加器fa封装2_16_p3 , \一位全加器fa封装2_20_p5 [0]
  // 一位全加器FA封装2 一位全加器fa封装2_21: pin names not known; wires that end beside it: \一位全加器fa封装2_17_p3 , \一位全加器fa封装2_11_p5 [0], \一位全加器fa封装2_21_p3 , \一位全加器fa封装2_21_p4 , \一位全加器fa封装2_17_p5 , 1'b0
  // 一位全加器FA封装2 一位全加器fa封装2_22: pin names not known; wires that end beside it: \一位全加器fa封装2_15_p5 [0], \一位全加器fa封装2_22_p2 , \一位全加器fa封装2_22_p3 , \一位全加器fa封装2_22_p4 , \一位全加器fa封装2_22_p5 
  // 一位全加器FA封装2 一位全加器fa封装2_23: pin names not known; wires that end beside it: \一位全加器fa封装2_16_p5 , \一位全加器fa封装2_23_p2 , \一位全加器fa封装2_23_p3 , \一位全加器fa封装2_22_p2 , \一位全加器fa封装2_23_p5 
  // 一位全加器FA封装2 一位全加器fa封装2_24: pin names not known; wires that end beside it: \一位全加器fa封装2_20_p5 [2], \一位全加器fa封装2_24_p2 , \一位全加器fa封装2_24_p3 , \一位全加器fa封装2_23_p2 , \一位全加器fa封装2_24_p5 
  shape shape_3 ();
  // 一位全加器FA封装2 一位全加器fa封装2_25: pin names not known; wires that end beside it: \一位全加器fa封装2_25_p1 , \一位全加器fa封装2_22_p4 , \一位全加器fa封装2_25_p5 [1], \一位全加器fa封装2_25_p4 , \一位全加器fa封装2_25_p5 [0]
  // 一位全加器FA封装2 一位全加器fa封装2_26: pin names not known; wires that end beside it: \一位全加器fa封装2_15_p5 [1], \一位全加器fa封装2_26_p5 [2], \一位全加器fa封装2_26_p5 [1], \一位全加器fa封装2_22_p3 , \一位全加器fa封装2_26_p5 [0]
  // 一位全加器FA封装2 一位全加器fa封装2_27: pin names not known; wires that end beside it: \一位全加器fa封装2_23_p3 , \一位全加器fa封装2_20_p5 [0], \一位全加器fa封装2_27_p3 , \一位全加器fa封装2_27_p4 , \一位全加器fa封装2_23_p5 , 1'b0
  // 一位全加器FA封装2 一位全加器fa封装2_28: pin names not known; wires that end beside it: \一位全加器fa封装2_23_p2 , \一位全加器fa封装2_20_p5 [1], \一位全加器fa封装2_28_p3 , \一位全加器fa封装2_28_p4 , \一位全加器fa封装2_23_p3 , \一位全加器fa封装2_28_p6 
  // 一位全加器FA封装2 一位全加器fa封装2_29: pin names not known; wires that end beside it: \一位全加器fa封装2_22_p5 , \一位全加器fa封装2_29_p2 , \一位全加器fa封装2_29_p3 , \一位全加器fa封装2_29_p4 , \一位全加器fa封装2_29_p5 
  // 一位全加器FA封装2 一位全加器fa封装2_30: pin names not known; wires that end beside it: \一位全加器fa封装2_26_p5 [2], \一位全加器fa封装2_30_p2 , \一位全加器fa封装2_30_p3 , \一位全加器fa封装2_29_p2 , \一位全加器fa封装2_30_p5 
  // 一位全加器FA封装2 一位全加器fa封装2_31: pin names not known; wires that end beside it: \一位全加器fa封装2_31_p1 , \一位全加器fa封装2_31_p2 , \一位全加器fa封装2_31_p5 [1], \一位全加器fa封装2_31_p4 , \一位全加器fa封装2_31_p5 [0]
  // 一位全加器FA封装2 一位全加器fa封装2_32: pin names not known; wires that end beside it: \一位全加器fa封装2_25_p5 [0], \一位全加器fa封装2_29_p4 , \一位全加器fa封装2_32_p3 , \一位全加器fa封装2_31_p2 , \一位全加器fa封装2_32_p5 
  // 一位全加器FA封装2 一位全加器fa封装2_33: pin names not known; wires that end beside it: \一位全加器fa封装2_25_p5 [1], \一位全加器fa封装2_33_p5 [2], \一位全加器fa封装2_33_p5 [1], \一位全加器fa封装2_32_p3 , \一位全加器fa封装2_33_p5 [0]
  // 一位全加器FA封装2 一位全加器fa封装2_34: pin names not known; wires that end beside it: \一位全加器fa封装2_29_p2 , \一位全加器fa封装2_26_p5 [1], \一位全加器fa封装2_34_p3 , \一位全加器fa封装2_34_p4 , \一位全加器fa封装2_29_p3 , \一位全加器fa封装2_34_p6 
  // 一位全加器FA封装2 一位全加器fa封装2_35: pin names not known; wires that end beside it: \一位全加器fa封装2_29_p3 , \一位全加器fa封装2_26_p5 [0], \一位全加器fa封装2_35_p3 , \一位全加器fa封装2_35_p4 , \一位全加器fa封装2_29_p5 , 1'b0
  // 一位全加器FA封装2 一位全加器fa封装2_36: pin names not known; wires that end beside it: \一位全加器fa封装2_33_p5 [2], \一位全加器fa封装2_36_p2 , \一位全加器fa封装2_36_p3 , \一位全加器fa封装2_36_p4 , \一位全加器fa封装2_36_p5 
  // 一位全加器FA封装2 一位全加器fa封装2_37: pin names not known; wires that end beside it: \一位全加器fa封装2_37_p1 , \一位全加器fa封装2_37_p2 , \一位全加器fa封装2_37_p5 [1], \一位全加器fa封装2_37_p4 , \一位全加器fa封装2_37_p5 [0]
  // 一位全加器FA封装2 一位全加器fa封装2_38: pin names not known; wires that end beside it: \一位全加器fa封装2_31_p5 [0], \一位全加器fa封装2_38_p2 , \一位全加器fa封装2_38_p3 , \一位全加器fa封装2_37_p2 , \一位全加器fa封装2_38_p5 
  // 一位全加器FA封装2 一位全加器fa封装2_39: pin names not known; wires that end beside it: \一位全加器fa封装2_31_p5 [1], \一位全加器fa封装2_39_p5 [2], \一位全加器fa封装2_39_p5 [1], \一位全加器fa封装2_38_p3 , \一位全加器fa封装2_39_p5 [0]
  // 一位全加器FA封装2 一位全加器fa封装2_40: pin names not known; wires that end beside it: \一位全加器fa封装2_32_p5 , \一位全加器fa封装2_36_p4 , \一位全加器fa封装2_40_p3 , \一位全加器fa封装2_38_p2 , \一位全加器fa封装2_40_p5 
  // 一位全加器FA封装2 一位全加器fa封装2_41: pin names not known; wires that end beside it: \一位全加器fa封装2_36_p4 , \一位全加器fa封装2_33_p5 [1], \一位全加器fa封装2_41_p3 , \一位全加器fa封装2_41_p4 , \一位全加器fa封装2_40_p3 , \一位全加器fa封装2_41_p6 
  shape shape_4 ();
  // 一位全加器FA封装2 一位全加器fa封装2_42: pin names not known; wires that end beside it: \一位全加器fa封装2_40_p3 , \一位全加器fa封装2_33_p5 [0], \一位全加器fa封装2_42_p3 , \一位全加器fa封装2_42_p4 , \一位全加器fa封装2_40_p5 , 1'b0
  // 一位全加器FA封装2 一位全加器fa封装2_43: pin names not known; wires that end beside it: \一位全加器fa封装2_43_p1 , \一位全加器fa封装2_43_p2 , \一位全加器fa封装2_43_p5 [1], \一位全加器fa封装2_43_p4 , \一位全加器fa封装2_43_p5 [0]
  // 一位全加器FA封装2 一位全加器fa封装2_44: pin names not known; wires that end beside it: \一位全加器fa封装2_37_p5 [0], \一位全加器fa封装2_44_p2 , \一位全加器fa封装2_44_p3 , \一位全加器fa封装2_43_p2 , \一位全加器fa封装2_44_p5 
  // 一位全加器FA封装2 一位全加器fa封装2_45: pin names not known; wires that end beside it: \一位全加器fa封装2_38_p5 , \一位全加器fa封装2_45_p2 , \一位全加器fa封装2_45_p3 , \一位全加器fa封装2_44_p2 , \一位全加器fa封装2_45_p5 
  // 一位全加器FA封装2 一位全加器fa封装2_46: pin names not known; wires that end beside it: \一位全加器fa封装2_45_p2 , \一位全加器fa封装2_39_p5 [1], \一位全加器fa封装2_46_p3 , \一位全加器fa封装2_46_p4 , \一位全加器fa封装2_45_p3 , \一位全加器fa封装2_46_p6 
  // 一位全加器FA封装2 一位全加器fa封装2_47: pin names not known; wires that end beside it: \一位全加器fa封装2_39_p5 [2], \一位全加器fa封装2_47_p2 , \一位全加器fa封装2_47_p3 , \一位全加器fa封装2_45_p2 , \一位全加器fa封装2_47_p5 
  // 一位全加器FA封装2 一位全加器fa封装2_48: pin names not known; wires that end beside it: \一位全加器fa封装2_37_p5 [1], \一位全加器fa封装2_48_p5 [2], \一位全加器fa封装2_48_p5 [1], \一位全加器fa封装2_44_p3 , \一位全加器fa封装2_48_p5 [0]
  // 一位全加器FA封装2 一位全加器fa封装2_49: pin names not known; wires that end beside it: \一位全加器fa封装2_45_p3 , \一位全加器fa封装2_39_p5 [0], \一位全加器fa封装2_49_p3 , \一位全加器fa封装2_49_p4 , \一位全加器fa封装2_45_p5 , 1'b0
  // 一位全加器FA封装2 一位全加器fa封装2_50: pin names not known; wires that end beside it: \一位全加器fa封装2_43_p5 [0], \一位全加器fa封装2_50_p2 , \一位全加器fa封装2_50_p3 , \一位全加器fa封装2_50_p4 , \一位全加器fa封装2_50_p5 
  // 一位全加器FA封装2 一位全加器fa封装2_51: pin names not known; wires that end beside it: \一位全加器fa封装2_44_p5 , \一位全加器fa封装2_51_p2 , \一位全加器fa封装2_51_p3 , \一位全加器fa封装2_50_p2 , \一位全加器fa封装2_51_p5 
  // 一位全加器FA封装2 一位全加器fa封装2_52: pin names not known; wires that end beside it: \一位全加器fa封装2_48_p5 [2], \一位全加器fa封装2_52_p2 , \一位全加器fa封装2_52_p3 , \一位全加器fa封装2_51_p2 , \一位全加器fa封装2_52_p5 
  shape shape_5 ();
  // 一位全加器FA封装2 一位全加器fa封装2_53: pin names not known; wires that end beside it: \一位全加器fa封装2_53_p1 , \一位全加器fa封装2_50_p4 , \一位全加器fa封装2_53_p5 [1], \一位全加器fa封装2_53_p4 , \一位全加器fa封装2_53_p5 [0]
  // 一位全加器FA封装2 一位全加器fa封装2_54: pin names not known; wires that end beside it: \一位全加器fa封装2_43_p5 [1], \一位全加器fa封装2_54_p5 [2], \一位全加器fa封装2_54_p5 [1], \一位全加器fa封装2_50_p3 , \一位全加器fa封装2_54_p5 [0]
  // 一位全加器FA封装2 一位全加器fa封装2_55: pin names not known; wires that end beside it: \一位全加器fa封装2_51_p2 , \一位全加器fa封装2_48_p5 [1], \一位全加器fa封装2_55_p3 , \一位全加器fa封装2_55_p4 , \一位全加器fa封装2_51_p3 , \一位全加器fa封装2_55_p6 
  // 一位全加器FA封装2 一位全加器fa封装2_56: pin names not known; wires that end beside it: \一位全加器fa封装2_51_p3 , \一位全加器fa封装2_48_p5 [0], \一位全加器fa封装2_56_p3 , \一位全加器fa封装2_56_p4 , \一位全加器fa封装2_51_p5 , 1'b0
  // 一位全加器FA封装2 一位全加器fa封装2_57: pin names not known; wires that end beside it: \一位全加器fa封装2_50_p5 , \一位全加器fa封装2_57_p2 , \一位全加器fa封装2_57_p3 , \一位全加器fa封装2_57_p4 , \一位全加器fa封装2_57_p5 
  // 一位全加器FA封装2 一位全加器fa封装2_58: pin names not known; wires that end beside it: \一位全加器fa封装2_54_p5 [2], \一位全加器fa封装2_58_p2 , \一位全加器fa封装2_58_p3 , \一位全加器fa封装2_57_p2 , \一位全加器fa封装2_58_p5 
  // 一位全加器FA封装2 一位全加器fa封装2_59: pin names not known; wires that end beside it: \一位全加器fa封装2_59_p1 , \一位全加器fa封装2_59_p2 , \一位全加器fa封装2_59_p5 [1], \一位全加器fa封装2_59_p4 , \一位全加器fa封装2_59_p5 [0]
  // 一位全加器FA封装2 一位全加器fa封装2_60: pin names not known; wires that end beside it: \一位全加器fa封装2_53_p5 [0], \一位全加器fa封装2_57_p4 , \一位全加器fa封装2_60_p3 , \一位全加器fa封装2_59_p2 , \一位全加器fa封装2_60_p5 
  // 一位全加器FA封装2 一位全加器fa封装2_61: pin names not known; wires that end beside it: \一位全加器fa封装2_53_p5 [1], \一位全加器fa封装2_61_p5 [2], \一位全加器fa封装2_61_p5 [1], \一位全加器fa封装2_60_p3 , \一位全加器fa封装2_61_p5 [0]
  // 一位全加器FA封装2 一位全加器fa封装2_62: pin names not known; wires that end beside it: \一位全加器fa封装2_57_p3 , \一位全加器fa封装2_54_p5 [0], \一位全加器fa封装2_62_p3 , \一位全加器fa封装2_62_p4 , \一位全加器fa封装2_57_p5 , 1'b0
  // 一位全加器FA封装2 一位全加器fa封装2_63: pin names not known; wires that end beside it: \一位全加器fa封装2_57_p2 , \一位全加器fa封装2_54_p5 [1], \一位全加器fa封装2_63_p3 , \一位全加器fa封装2_63_p4 , \一位全加器fa封装2_57_p3 , \一位全加器fa封装2_63_p6 
  // 一位全加器FA封装2 一位全加器fa封装2_64: pin names not known; wires that end beside it: \一位全加器fa封装2_61_p5 [2], \一位全加器fa封装2_64_p2 , \一位全加器fa封装2_64_p3 , \一位全加器fa封装2_64_p4 , \一位全加器fa封装2_64_p5 
  // 一位全加器FA封装2 一位全加器fa封装2_65: pin names not known; wires that end beside it: \一位全加器fa封装2_65_p1 , \一位全加器fa封装2_65_p2 , \一位全加器fa封装2_65_p5 [1], \一位全加器fa封装2_65_p4 , \一位全加器fa封装2_65_p5 [0]
  // 一位全加器FA封装2 一位全加器fa封装2_66: pin names not known; wires that end beside it: \一位全加器fa封装2_59_p5 [0], \一位全加器fa封装2_66_p2 , \一位全加器fa封装2_66_p3 , \一位全加器fa封装2_65_p2 , \一位全加器fa封装2_66_p5 
  // 一位全加器FA封装2 一位全加器fa封装2_67: pin names not known; wires that end beside it: \一位全加器fa封装2_59_p5 [1], \一位全加器fa封装2_67_p5 [2], \一位全加器fa封装2_67_p5 [1], \一位全加器fa封装2_66_p3 , \一位全加器fa封装2_67_p5 [0]
  // 一位全加器FA封装2 一位全加器fa封装2_68: pin names not known; wires that end beside it: \一位全加器fa封装2_60_p5 , \一位全加器fa封装2_64_p4 , \一位全加器fa封装2_68_p3 , \一位全加器fa封装2_66_p2 , \一位全加器fa封装2_68_p5 
  // 一位全加器FA封装2 一位全加器fa封装2_69: pin names not known; wires that end beside it: \一位全加器fa封装2_64_p4 , \一位全加器fa封装2_61_p5 [1], \一位全加器fa封装2_69_p3 , \一位全加器fa封装2_69_p4 , \一位全加器fa封装2_68_p3 , \一位全加器fa封装2_69_p6 
  shape shape_6 ();
  // 一位全加器FA封装2 一位全加器fa封装2_70: pin names not known; wires that end beside it: \一位全加器fa封装2_68_p3 , \一位全加器fa封装2_61_p5 [0], \一位全加器fa封装2_70_p3 , \一位全加器fa封装2_70_p4 , \一位全加器fa封装2_68_p5 , 1'b0
  // 一位全加器FA封装2 一位全加器fa封装2_71: pin names not known; wires that end beside it: \一位全加器fa封装2_71_p1 , \一位全加器fa封装2_71_p2 , \一位全加器fa封装2_71_p5 [1], \一位全加器fa封装2_71_p4 , \一位全加器fa封装2_71_p5 [0]
  // 一位全加器FA封装2 一位全加器fa封装2_72: pin names not known; wires that end beside it: \一位全加器fa封装2_65_p5 [0], \一位全加器fa封装2_72_p2 , \一位全加器fa封装2_72_p3 , \一位全加器fa封装2_71_p2 , \一位全加器fa封装2_72_p5 
  // 一位全加器FA封装2 一位全加器fa封装2_73: pin names not known; wires that end beside it: \一位全加器fa封装2_66_p5 , \一位全加器fa封装2_73_p2 , \一位全加器fa封装2_73_p3 , \一位全加器fa封装2_72_p2 , \一位全加器fa封装2_73_p5 
  // 一位全加器FA封装2 一位全加器fa封装2_74: pin names not known; wires that end beside it: \一位全加器fa封装2_73_p2 , \一位全加器fa封装2_67_p5 [1], \一位全加器fa封装2_74_p3 , \一位全加器fa封装2_74_p4 , \一位全加器fa封装2_73_p3 , \一位全加器fa封装2_74_p6 
  // 一位全加器FA封装2 一位全加器fa封装2_75: pin names not known; wires that end beside it: \一位全加器fa封装2_67_p5 [2], \一位全加器fa封装2_75_p2 , \一位全加器fa封装2_75_p3 , \一位全加器fa封装2_73_p2 , \一位全加器fa封装2_75_p5 
  // 一位全加器FA封装2 一位全加器fa封装2_76: pin names not known; wires that end beside it: \一位全加器fa封装2_65_p5 [1], \一位全加器fa封装2_76_p5 [2], \一位全加器fa封装2_76_p5 [1], \一位全加器fa封装2_72_p3 , \一位全加器fa封装2_76_p5 [0]
  // 一位全加器FA封装2 一位全加器fa封装2_77: pin names not known; wires that end beside it: \一位全加器fa封装2_73_p3 , \一位全加器fa封装2_67_p5 [0], \一位全加器fa封装2_77_p3 , \一位全加器fa封装2_77_p4 , \一位全加器fa封装2_73_p5 , 1'b0
  // 一位全加器FA封装2 一位全加器fa封装2_78: pin names not known; wires that end beside it: \一位全加器fa封装2_71_p5 [0], \一位全加器fa封装2_78_p2 , \一位全加器fa封装2_78_p3 , \一位全加器fa封装2_78_p4 , \一位全加器fa封装2_78_p5 
  // 一位全加器FA封装2 一位全加器fa封装2_79: pin names not known; wires that end beside it: \一位全加器fa封装2_72_p5 , \一位全加器fa封装2_79_p2 , \一位全加器fa封装2_79_p3 , \一位全加器fa封装2_78_p2 , \一位全加器fa封装2_79_p5 
  // 一位全加器FA封装2 一位全加器fa封装2_80: pin names not known; wires that end beside it: \一位全加器fa封装2_76_p5 [2], \一位全加器fa封装2_80_p2 , \一位全加器fa封装2_80_p3 , \一位全加器fa封装2_79_p2 , \一位全加器fa封装2_80_p5 
  shape shape_7 ();
  // 一位全加器FA封装2 一位全加器fa封装2_81: pin names not known; wires that end beside it: \一位全加器fa封装2_81_p1 , \一位全加器fa封装2_78_p4 , \一位全加器fa封装2_81_p5 [1], \一位全加器fa封装2_81_p4 , \一位全加器fa封装2_81_p5 [0]
  // 一位全加器FA封装2 一位全加器fa封装2_82: pin names not known; wires that end beside it: \一位全加器fa封装2_71_p5 [1], \一位全加器fa封装2_82_p5 [2], \一位全加器fa封装2_82_p5 [1], \一位全加器fa封装2_78_p3 , \一位全加器fa封装2_82_p5 [0]
  // 一位全加器FA封装2 一位全加器fa封装2_83: pin names not known; wires that end beside it: \一位全加器fa封装2_79_p2 , \一位全加器fa封装2_76_p5 [1], \一位全加器fa封装2_83_p3 , \一位全加器fa封装2_83_p4 , \一位全加器fa封装2_79_p3 , \一位全加器fa封装2_83_p6 
  // 一位全加器FA封装2 一位全加器fa封装2_84: pin names not known; wires that end beside it: \一位全加器fa封装2_79_p3 , \一位全加器fa封装2_76_p5 [0], \一位全加器fa封装2_84_p3 , \一位全加器fa封装2_84_p4 , \一位全加器fa封装2_79_p5 , 1'b0
  // 一位全加器FA封装2 一位全加器fa封装2_85: pin names not known; wires that end beside it: \一位全加器fa封装2_78_p5 , \一位全加器fa封装2_85_p2 , \一位全加器fa封装2_85_p3 , \一位全加器fa封装2_85_p4 , \一位全加器fa封装2_85_p5 
  // 一位全加器FA封装2 一位全加器fa封装2_86: pin names not known; wires that end beside it: \一位全加器fa封装2_82_p5 [2], \一位全加器fa封装2_86_p2 , \一位全加器fa封装2_86_p3 , \一位全加器fa封装2_85_p2 , \一位全加器fa封装2_86_p5 
  // 一位全加器FA封装2 一位全加器fa封装2_87: pin names not known; wires that end beside it: \一位全加器fa封装2_87_p1 , \一位全加器fa封装2_87_p2 , \一位全加器fa封装2_87_p5 [1], \一位全加器fa封装2_87_p4 , \一位全加器fa封装2_87_p5 [0]
  // 一位全加器FA封装2 一位全加器fa封装2_88: pin names not known; wires that end beside it: \一位全加器fa封装2_81_p5 [0], \一位全加器fa封装2_85_p4 , \一位全加器fa封装2_88_p3 , \一位全加器fa封装2_87_p2 , \一位全加器fa封装2_88_p5 
  // 一位全加器FA封装2 一位全加器fa封装2_89: pin names not known; wires that end beside it: \一位全加器fa封装2_81_p5 [1], \一位全加器fa封装2_89_p5 [2], \一位全加器fa封装2_89_p5 [1], \一位全加器fa封装2_88_p3 , \一位全加器fa封装2_89_p5 [0]
  // 一位全加器FA封装2 一位全加器fa封装2_90: pin names not known; wires that end beside it: \一位全加器fa封装2_85_p2 , \一位全加器fa封装2_82_p5 [1], \一位全加器fa封装2_90_p3 , \一位全加器fa封装2_90_p4 , \一位全加器fa封装2_85_p3 , \一位全加器fa封装2_90_p6 
  // 一位全加器FA封装2 一位全加器fa封装2_91: pin names not known; wires that end beside it: \一位全加器fa封装2_85_p3 , \一位全加器fa封装2_82_p5 [0], \一位全加器fa封装2_91_p3 , \一位全加器fa封装2_91_p4 , \一位全加器fa封装2_85_p5 , 1'b0
  // 一位全加器FA封装2 一位全加器fa封装2_92: pin names not known; wires that end beside it: \一位全加器fa封装2_89_p5 [2], \一位全加器fa封装2_92_p2 , \一位全加器fa封装2_92_p3 , \一位全加器fa封装2_92_p4 , \一位全加器fa封装2_92_p5 
  // 一位全加器FA封装2 一位全加器fa封装2_93: pin names not known; wires that end beside it: \一位全加器fa封装2_93_p1 , \一位全加器fa封装2_93_p2 , \一位全加器fa封装2_93_p5 [1], \一位全加器fa封装2_93_p4 , \一位全加器fa封装2_93_p5 [0]
  // 一位全加器FA封装2 一位全加器fa封装2_94: pin names not known; wires that end beside it: \一位全加器fa封装2_87_p5 [0], \一位全加器fa封装2_94_p2 , \一位全加器fa封装2_94_p3 , \一位全加器fa封装2_93_p2 , \一位全加器fa封装2_94_p5 
  // 一位全加器FA封装2 一位全加器fa封装2_95: pin names not known; wires that end beside it: \一位全加器fa封装2_87_p5 [1], \一位全加器fa封装2_95_p5 [2], \一位全加器fa封装2_95_p5 [1], \一位全加器fa封装2_94_p3 , \一位全加器fa封装2_95_p5 [0]
  // 一位全加器FA封装2 一位全加器fa封装2_96: pin names not known; wires that end beside it: \一位全加器fa封装2_88_p5 , \一位全加器fa封装2_92_p4 , \一位全加器fa封装2_96_p3 , \一位全加器fa封装2_94_p2 , \一位全加器fa封装2_96_p5 
  // 一位全加器FA封装2 一位全加器fa封装2_97: pin names not known; wires that end beside it: \一位全加器fa封装2_92_p4 , \一位全加器fa封装2_89_p5 [1], \一位全加器fa封装2_97_p3 , \一位全加器fa封装2_97_p4 , \一位全加器fa封装2_96_p3 , \一位全加器fa封装2_97_p6 
  shape shape_8 ();
  // 一位全加器FA封装2 一位全加器fa封装2_98: pin names not known; wires that end beside it: \一位全加器fa封装2_96_p3 , \一位全加器fa封装2_89_p5 [0], \一位全加器fa封装2_98_p3 , \一位全加器fa封装2_98_p4 , \一位全加器fa封装2_96_p5 , 1'b0
  // 一位全加器FA封装2 一位全加器fa封装2_99: pin names not known; wires that end beside it: \一位全加器fa封装2_99_p1 , \一位全加器fa封装2_99_p2 , \一位全加器fa封装2_99_p5 [1], \一位全加器fa封装2_99_p4 , \一位全加器fa封装2_99_p5 [0]
  // 一位全加器FA封装2 一位全加器fa封装2_100: pin names not known; wires that end beside it: \一位全加器fa封装2_93_p5 [0], \一位全加器fa封装2_100_p2 , \一位全加器fa封装2_100_p3 , \一位全加器fa封装2_99_p2 , \一位全加器fa封装2_100_p5 
  // 一位全加器FA封装2 一位全加器fa封装2_101: pin names not known; wires that end beside it: \一位全加器fa封装2_94_p5 , \一位全加器fa封装2_101_p2 , \一位全加器fa封装2_101_p3 , \一位全加器fa封装2_100_p2 , \一位全加器fa封装2_101_p5 
  // 一位全加器FA封装2 一位全加器fa封装2_102: pin names not known; wires that end beside it: \一位全加器fa封装2_95_p5 [2], \一位全加器fa封装2_102_p2 , \一位全加器fa封装2_102_p3 , \一位全加器fa封装2_101_p2 , \一位全加器fa封装2_102_p5 
  // 一位全加器FA封装2 一位全加器fa封装2_103: pin names not known; wires that end beside it: \一位全加器fa封装2_101_p2 , \一位全加器fa封装2_95_p5 [1], \一位全加器fa封装2_103_p3 , \一位全加器fa封装2_103_p4 , \一位全加器fa封装2_101_p3 , \一位全加器fa封装2_103_p6 
  // 一位全加器FA封装2 一位全加器fa封装2_104: pin names not known; wires that end beside it: \一位全加器fa封装2_93_p5 [1], \一位全加器fa封装2_104_p5 [2], \一位全加器fa封装2_104_p5 [1], \一位全加器fa封装2_100_p3 , \一位全加器fa封装2_104_p5 [0]
  // 一位全加器FA封装2 一位全加器fa封装2_105: pin names not known; wires that end beside it: \一位全加器fa封装2_101_p3 , \一位全加器fa封装2_95_p5 [0], \一位全加器fa封装2_105_p3 , \一位全加器fa封装2_105_p4 , \一位全加器fa封装2_101_p5 , 1'b0
  // 一位全加器FA封装2 一位全加器fa封装2_106: pin names not known; wires that end beside it: \一位全加器fa封装2_99_p5 [0], \一位全加器fa封装2_106_p2 , \一位全加器fa封装2_106_p3 , \一位全加器fa封装2_106_p4 , \一位全加器fa封装2_106_p5 
  // 一位全加器FA封装2 一位全加器fa封装2_107: pin names not known; wires that end beside it: \一位全加器fa封装2_100_p5 , \一位全加器fa封装2_107_p2 , \一位全加器fa封装2_107_p3 , \一位全加器fa封装2_106_p2 , \一位全加器fa封装2_107_p5 
  // 一位全加器FA封装2 一位全加器fa封装2_108: pin names not known; wires that end beside it: \一位全加器fa封装2_104_p5 [2], \一位全加器fa封装2_108_p2 , \一位全加器fa封装2_108_p3 , \一位全加器fa封装2_107_p2 , \一位全加器fa封装2_108_p5 
  // 一位全加器FA封装2 一位全加器fa封装2_109: pin names not known; wires that end beside it: \一位全加器fa封装2_109_p1 , \一位全加器fa封装2_106_p4 , \一位全加器fa封装2_109_p5 [1], \一位全加器fa封装2_109_p4 , \一位全加器fa封装2_109_p5 [0]
  // 一位全加器FA封装2 一位全加器fa封装2_110: pin names not known; wires that end beside it: \一位全加器fa封装2_99_p5 [1], \一位全加器fa封装2_110_p5 [2], \一位全加器fa封装2_110_p5 [1], \一位全加器fa封装2_106_p3 , \一位全加器fa封装2_110_p5 [0]
  // 一位全加器FA封装2 一位全加器fa封装2_111: pin names not known; wires that end beside it: \一位全加器fa封装2_107_p3 , \一位全加器fa封装2_104_p5 [0], \一位全加器fa封装2_111_p3 , \一位全加器fa封装2_111_p4 , \一位全加器fa封装2_107_p5 , 1'b0, \一位全加器fa封装2_110_p5 
  // 一位全加器FA封装2 一位全加器fa封装2_112: pin names not known; wires that end beside it: \一位全加器fa封装2_107_p2 , \一位全加器fa封装2_104_p5 [1], \一位全加器fa封装2_112_p3 , \一位全加器fa封装2_112_p4 , \一位全加器fa封装2_107_p3 , \一位全加器fa封装2_112_p6 
endmodule

// Trace
module trace (
  input  [7:0] in_1,
  output [31:0] X,
  output [31:0] Y,
  output [3:0] AluOP,
  output [31:0] R,
  output [31:0] R2,
  output [2:0] FLAGS
);

  ROM #(.dataWidth(32)) rom_1 (.addr(in_1), .data(X));  // open: sel
  ROM #(.dataWidth(32)) rom_2 (.addr(in_1), .data(Y));  // open: sel
  ROM #(.dataWidth(4)) rom_3 (.addr(in_1), .data(AluOP));  // open: sel
  ROM #(.dataWidth(32)) rom_4 (.addr(in_1), .data(R));  // open: sel
  ROM #(.dataWidth(32)) rom_5 (.addr(in_1), .data(R2));  // open: sel
  ROM #(.dataWidth(3)) rom_6 (.addr(in_1), .data(FLAGS));  // open: sel

  // Notes on the sheet:
  //   X trace
  //   Y trace
  //   ALU OP Trace
  //   Result Benchmark
  //   Result2 Benchmark
  //   FLAGS Benchmark
  //   contents of rom_1 (hex, n*v repeats v):
  //   ff00ffff ff00ffff ff000000 ff00ffff 7fffffff fffffffe ffff ffffffff 7fffffff 80000000 7ff00000 7c
  //   80000000 7fffffff ff00ffff 7fffffff 18*fffffffe
  //   contents of rom_2 (hex, n*v repeats v):
  //   7 ff00ffff 18 18 10 10 80 ffffffff c 80000000 7c 7ff00000 1 fffffffe 18 74 fffffffe 88 10 ffffffff
  //   10 ffffffff 12*10
  //   contents of rom_3 (hex, n*v repeats v):
  //   0 0 1 2 3 4 4*5 4*6 7 8 9 a b b c c f 11*9 f
  //   contents of rom_4 (hex, n*v repeats v):
  //   807fff80 80000000 ffffffff ff fffffff0 fffffff 1007f fffffffe 8000000b 0 7fefff84 8010007c 7fffffff
  //   80000001 18 7fffffff 0 1 1 1 0 1 300000 11*ffffffee 1
  //   contents of rom_5 (hex, n*v repeats v):
  //   4*0 7 e
  //   contents of rom_6 (hex, n*v repeats v):
  //   0 1 5*0 3 4 7 0 2 4 6 0 0 1 17*0 66*1
endmodule

// 单项评分
module \单项评分  (
  input  ALU_SWITCH,
  input  EQ,
  input  EN,
  input  [4:0] \分值 ,
  input  CLK,
  output [7:0] \正确条数 ,
  output [7:0] \扣分 ,
  output Right,
  output [7:0] Total
);

  wire and_1_out, and_2_out, not_1_out, priority_encoder_1_gs, priority_encoder_1_out;
  wire [7:0] bit_extender_1_out;

  and and_1 (and_1_out, ALU_SWITCH, EN);
  Priority_Encoder #(.select(1)) priority_encoder_1 (
    .in0(EQ), .in1(EQ), .out(priority_encoder_1_out), .gs(priority_encoder_1_gs));  // open: en_out, en_in
  Counter counter_1 (.count(and_1_out), .Q(Total), .clk(CLK));  // open: load, D, carry, clr
  and and_2 (and_2_out, ALU_SWITCH, priority_encoder_1_out, priority_encoder_1_gs, EN);
  Counter counter_2 (.count(and_2_out), .Q(\正确条数 ), .clk(CLK));  // open: load, D, carry, clr
  Comparator comparator_1 (.a(\正确条数 ), .b(Total), .eq(Right));  // open: gt, lt
  assign bit_extender_1_out = {{3{1'b0}}, \分值 };  // Bit_Extender bit_extender_1
  Multiplexer #(.width(8), .enable("false")) multiplexer_1 (
    .in0({8{1'b0}}), .in1(bit_extender_1_out), .out(\扣分 ), .sel(not_1_out));
  not not_1 (not_1_out, Right);

  // Notes on the sheet:
  //   只有使用优先编码器才能屏蔽掉位置状态
endmodule

module \总评分  (
  input  [7:0] in_1,
  input  [7:0] in_2,
  input  [7:0] in_3,
  input  [7:0] in_4,
  input  [7:0] in_5,
  input  [7:0] in_6,
  input  [7:0] in_7,
  input  [7:0] in_8,
  input  [7:0] in_9,
  input  [7:0] in_10,
  input  [7:0] in_11,
  input  [7:0] in_12,
  input  [7:0] in_13,
  input  [7:0] in_14,
  input  [7:0] in_15,
  input  [7:0] in_16,
  input  \悬空扣分 ,
  output [7:0] Result,
  output [3:0] High,
  output [3:0] Low,
  output [3:0] Mid
);

  wire [7:0] adder_1_out, adder_2_out, adder_3_out, adder_4_out, adder_5_out, adder_6_out, adder_7_out,
       adder_8_out, adder_9_out, adder_10_out, adder_11_out, adder_12_out, adder_13_out, adder_14_out,
       adder_15_out, divider_1_out, subtractor_1_out, subtractor_2_out;
  wire [7:4] divider_1_rem, divider_2_out, divider_2_rem;

  Adder adder_1 (.a(in_1), .b(in_2), .out(adder_1_out));  // open: cin, cout
  Adder adder_2 (.a(in_3), .b(in_4), .out(adder_2_out));  // open: cin, cout
  Adder adder_3 (.a(in_5), .b(in_6), .out(adder_3_out));  // open: cin, cout
  Adder adder_4 (.a(in_7), .b(in_8), .out(adder_4_out));  // open: cin, cout
  Adder adder_5 (.a(in_9), .b(in_10), .out(adder_5_out));  // open: cin, cout
  Adder adder_6 (.a(in_11), .b(in_12), .out(adder_6_out));  // open: cin, cout
  Adder adder_7 (.a(in_13), .b(in_14), .out(adder_7_out));  // open: cin, cout
  Adder adder_8 (.a(in_15), .b(in_16), .out(adder_8_out));  // open: cin, cout
  Adder adder_9 (.a(adder_1_out), .b(adder_2_out), .out(adder_9_out));  // open: cin, cout
  Adder adder_10 (.a(adder_3_out), .b(adder_4_out), .out(adder_10_out));  // open: cin, cout
  Adder adder_11 (.a(adder_5_out), .b(adder_6_out), .out(adder_11_out));  // open: cin, cout
  Adder adder_12 (.a(adder_7_out), .b(adder_8_out), .out(adder_12_out));  // open: cin, cout
  Adder adder_13 (.a(adder_9_out), .b(adder_10_out), .out(adder_13_out));  // open: cin, cout
  Adder adder_14 (.a(adder_11_out), .b(adder_12_out), .out(adder_14_out));  // open: cin, cout
  Adder adder_15 (.a(adder_13_out), .b(adder_14_out), .out(adder_15_out));  // open: cin, cout
  Subtractor subtractor_1 (.a(8'h64), .b(adder_15_out), .out(subtractor_1_out));  // open: bin, bout
  Subtractor subtractor_2 (.a(subtractor_1_out), .b(8'h5), .out(subtractor_2_out));  // open: bin, bout
  Multiplexer #(.width(8), .enable("false")) multiplexer_1 (
    .in0(subtractor_1_out), .in1(subtractor_2_out), .out(Result), .sel(\悬空扣分 ));
  Divider divider_1 (.a(Result), .b(8'ha), .out(divider_1_out), .rem({divider_1_rem, Low}));  // open: upper
  Divider divider_2 (
    .a(divider_1_out), .b(8'ha), .out({divider_2_out, High}), .rem({divider_2_rem, Mid}));  // open: upper
endmodule
